// Digital circuit Template.dig as structural Verilog
module Template (
  input  A,
  input  B,
  output Output
);

  wire and_1_out, and_2_out, not_1_out, not_2_out, or_1_out;

  not not_1 (not_1_out, A);
  not not_2 (not_2_out, B);
  and and_1 (and_1_out, B, A);
  and and_2 (and_2_out, not_1_out, not_2_out);
  or or_1 (or_1_out, and_1_out, and_2_out);
  not not_3 (Output, or_1_out);
endmodule
