// Digital circuit Template-03.dig as structural Verilog
module Template_03 (
  input  [3:0] In,
  input  [1:0] Selector,
  output [3:0] Output
);

  wire and_1_out, and_2_out, and_3_out, and_4_out, and_5_out, and_6_out, and_7_out, and_8_out, and_9_out,
       and_10_out, and_11_out, and_12_out, and_13_out, and_14_out, and_15_out, and_16_out, and_17_out,
       and_18_out, and_19_out, and_20_out, and_21_out, and_22_out, and_23_out, and_24_out, and_25_out,
       and_26_out, and_27_out, and_28_out, and_29_out, and_30_out, and_31_out, and_32_out, and_33_out,
       and_34_out, and_35_out, and_36_out, and_37_out, not_1_out, not_2_out, not_3_out, not_4_out, not_5_out,
       not_6_out, not_7_out, not_8_out, not_9_out, not_10_out, not_11_out, not_12_out, not_13_out,
       not_14_out, not_15_out, not_16_out, not_17_out, not_18_out, not_19_out, not_20_out, not_21_out,
       not_22_out, not_23_out, not_24_out, not_25_out, not_26_out, not_27_out, not_28_out, not_29_out,
       not_30_out, not_31_out;
  wire [2:0] c;
  wire [3:0] b, d, e;

  not not_1 (not_1_out, In[1]);
  not not_2 (not_2_out, In[2]);
  not not_3 (not_3_out, In[1]);
  not not_4 (not_4_out, In[1]);
  not not_5 (not_5_out, In[1]);
  not not_6 (not_6_out, In[0]);
  not not_7 (not_7_out, In[0]);
  not not_8 (not_8_out, In[0]);
  and and_1 (and_1_out, In[2], In[1]);
  and and_2 (and_2_out, In[2], not_1_out, In[0]);
  and and_3 (and_3_out, not_2_out, In[1]);
  and and_4 (and_4_out, not_2_out, not_3_out, In[0]);
  and and_5 (and_5_out, In[2], not_3_out, not_6_out);
  and and_6 (and_6_out, not_4_out, not_7_out);
  and and_7 (and_7_out, In[1], In[0]);
  and and_8 (and_8_out, not_5_out, not_8_out);
  and and_9 (and_9_out, In[1], not_8_out);
  or or_1 (b[3], In[3], and_1_out, and_2_out);
  or or_2 (b[2], and_3_out, and_4_out, and_5_out);
  or or_3 (b[1], and_6_out, and_7_out);
  or or_4 (b[0], and_8_out, and_9_out);
  not not_9 (not_9_out, In[2]);
  not not_10 (not_10_out, In[2]);
  Multiplexer #(.Selector_Bits(2), .Bits(4)) multiplexer_1 (
    .sel(Selector), .in_0(b), .in_1({In[3], c}), .in_2(d), .in_3(e), .out(Output));
  not not_11 (not_11_out, In[1]);
  not not_12 (not_12_out, In[1]);
  not not_13 (not_13_out, In[1]);
  not not_14 (not_14_out, In[0]);
  and and_10 (and_10_out, In[2], not_11_out, not_14_out);
  and and_11 (and_11_out, In[2], In[1]);
  and and_12 (and_12_out, In[2], not_11_out, In[0]);
  not not_15 (not_15_out, In[0]);
  and and_13 (and_13_out, not_9_out, In[1]);
  and and_14 (and_14_out, In[2], not_12_out, not_15_out);
  and and_15 (and_15_out, In[2], not_12_out, In[0]);
  not not_16 (not_16_out, In[0]);
  and and_16 (and_16_out, not_10_out, not_13_out, In[0]);
  and and_17 (and_17_out, In[2], not_13_out, In[0]);
  and and_18 (and_18_out, In[1], not_16_out);
  or or_5 (c[2], In[3], and_10_out, and_11_out, and_12_out);
  or or_6 (c[1], and_13_out, and_14_out, and_15_out);
  or or_7 (c[0], and_16_out, and_17_out, and_18_out);
  not not_17 (not_17_out, In[2]);
  not not_18 (not_18_out, In[2]);
  not not_19 (not_19_out, In[1]);
  not not_20 (not_20_out, In[1]);
  not not_21 (not_21_out, In[0]);
  not not_22 (not_22_out, In[1]);
  not not_23 (not_23_out, In[1]);
  and and_19 (and_19_out, In[2], In[1]);
  and and_20 (and_20_out, In[2], not_19_out, In[0]);
  and and_21 (and_21_out, In[2], not_20_out, not_21_out);
  and and_22 (and_22_out, In[2], In[1]);
  and and_23 (and_23_out, not_17_out, In[1]);
  and and_24 (and_24_out, In[2], not_22_out, In[0]);
  and and_25 (and_25_out, not_18_out, not_23_out, In[0]);
  and and_26 (and_26_out, In[2], not_23_out, In[0]);
  and and_27 (and_27_out, In[1], In[0]);
  or or_8 (d[3], In[3], and_19_out, and_20_out);
  or or_9 (d[2], In[3], and_21_out, and_22_out);
  or or_10 (d[1], In[3], and_23_out, and_24_out);
  or or_11 (d[0], and_25_out, and_26_out, and_27_out);
  not not_24 (not_24_out, In[1]);
  not not_25 (not_25_out, In[2]);
  not not_26 (not_26_out, In[1]);
  not not_27 (not_27_out, In[1]);
  not not_28 (not_28_out, In[2]);
  not not_29 (not_29_out, In[1]);
  not not_30 (not_30_out, In[0]);
  not not_31 (not_31_out, In[0]);
  and and_28 (and_28_out, In[2], not_24_out, In[0]);
  and and_29 (and_29_out, In[1], In[0]);
  and and_30 (and_30_out, not_25_out, not_26_out, In[0]);
  and and_31 (and_31_out, In[2], not_26_out, not_30_out);
  and and_32 (and_32_out, In[2], In[1]);
  and and_33 (and_33_out, In[2], not_27_out, In[0]);
  and and_34 (and_34_out, In[1], not_31_out);
  and and_35 (and_35_out, not_28_out, not_29_out, In[0]);
  and and_36 (and_36_out, In[2], not_29_out, In[0]);
  and and_37 (and_37_out, In[1], In[0]);
  or or_12 (e[3], In[3], and_28_out, and_29_out);
  or or_13 (e[2], and_30_out, and_31_out, and_32_out);
  or or_14 (e[1], In[3], and_33_out, and_34_out);
  or or_15 (e[0], and_35_out, and_36_out, and_37_out);

  // Other names for the same wires on the sheet: a[3:0] = In; c[3] = In[3]
endmodule
