// Digital circuit Template-04.dig as structural Verilog
module Template_04 (
  input  [6:0] In,
  output [6:0] Output
);

  wire demultiplexer_1_out_1, demultiplexer_1_out_2, demultiplexer_1_out_3, demultiplexer_1_out_4,
       demultiplexer_1_out_5, demultiplexer_1_out_6, demultiplexer_1_out_7;
  wire [2:0] xor_1_out;

  xor xor_1 (xor_1_out[2], In[3], In[2], In[1], In[0]);
  xor xor_2 (xor_1_out[1], In[5], In[4], In[1], In[0]);
  xor xor_3 (xor_1_out[0], In[6], In[4], In[2], In[0]);
  Demultiplexer #(.Selector_Bits(3)) demultiplexer_1 (
    .sel(xor_1_out), .in(1'b1), .out_1(demultiplexer_1_out_1), .out_2(demultiplexer_1_out_2),
    .out_3(demultiplexer_1_out_3), .out_4(demultiplexer_1_out_4), .out_5(demultiplexer_1_out_5),
    .out_6(demultiplexer_1_out_6), .out_7(demultiplexer_1_out_7));  // open: out_0
  xor xor_4 (Output[6], demultiplexer_1_out_1, In[6]);
  xor xor_5 (Output[5], demultiplexer_1_out_2, In[5]);
  xor xor_6 (Output[4], demultiplexer_1_out_3, In[4]);
  xor xor_7 (Output[3], demultiplexer_1_out_4, In[3]);
  xor xor_8 (Output[2], demultiplexer_1_out_5, In[2]);
  xor xor_9 (Output[1], demultiplexer_1_out_6, In[1]);
  xor xor_10 (Output[0], demultiplexer_1_out_7, In[0]);
endmodule
