// Digital circuit Template.dig as structural Verilog
module Template (
  input  T,
  input  Clear,
  input  Clock,
  output Q,
  output Q_2
);

  wire nor_1_out, nor_2_out, nor_3_out, nor_4_out, nor_5_out, not_1_out, not_2_out, xor_1_out;

  xor xor_1 (xor_1_out, T, Q);
  not not_1 (not_1_out, xor_1_out);
  not not_2 (not_2_out, Clock);
  nor nor_1 (nor_1_out, Clear, not_1_out);
  nor nor_2 (nor_2_out, nor_5_out, nor_3_out);
  nor nor_3 (nor_3_out, nor_2_out, not_2_out);
  nor nor_4 (nor_4_out, nor_3_out, not_2_out, nor_5_out);
  nor nor_5 (nor_5_out, nor_4_out, nor_1_out);
  nor nor_6 (Q, nor_3_out, Q_2);
  nor nor_7 (Q_2, Q, nor_4_out);
endmodule
