// Digital circuit Template.dig as structural Verilog
module Template (
  input  P5,
  input  reset,
  input  clock,
  input  P10,
  input  P20,
  input  Pcoffee,
  input  Ptea,
  input  Pchange,
  input  Pnext,
  output [5:0] Balance,
  output CoffeeOut,
  output TeaOut,
  output [1:0] Change5,
  output [1:0] Change10,
  output [1:0] Change20
);

  wire and_1_out, and_2_out, and_3_out, and_4_out, and_5_out, and_6_out, and_7_out, and_8_out, and_9_out,
       and_10_out, and_11_out, and_12_out, and_13_out, and_14_out, and_15_out, and_16_out, and_17_out,
       and_18_out, and_19_out, and_20_out, and_21_out, comparator_1_eq, comparator_2_eq, comparator_3_eq,
       comparator_4_eq, comparator_5_eq, comparator_6_eq, comparator_7_eq, comparator_8_eq, comparator_9_eq,
       comparator_10_eq, comparator_11_lt, comparator_12_gt, comparator_13_gt, comparator_14_lt,
       comparator_15_gt, comparator_16_gt, comparator_17_gt, comparator_18_lt, d_ff_7_nq, d_ff_8_nq,
       d_ff_9_nq, d_ff_10_nq, d_ff_11_nq, d_ff_12_nq, d_ff_13_nq, lookuptable_1_out, lookuptable_2_out,
       multiplexer_4_out, multiplexer_5_out, multiplexer_9_out, multiplexer_10_out, not_1_out, or_1_out,
       or_2_out, or_3_out, or_4_out, or_5_out, P5_t, P10_t, P20_t, Pchange_t, Pcoffee_t, Pnext_t, Ptea_t;
  wire [1:0] add_1_s, add_2_s, add_3_s, multiplexer_1_out, multiplexer_2_out, multiplexer_3_out,
       multiplexer_6_out, multiplexer_7_out, multiplexer_8_out;
  wire [4:0] multiplexer_13_out, multiplexer_14_out, multiplexer_16_out, multiplexer_18_out,
       multiplexer_19_out, multiplexer_20_out, multiplexer_21_out, multiplexer_22_out, multiplexer_23_out,
       multiplexer_24_out, multiplexer_25_out, multiplexer_26_out, multiplexer_27_out, multiplexer_28_out,
       multiplexer_29_out, State;
  wire [5:0] add_4_s, multiplexer_11_out, multiplexer_12_out, multiplexer_15_out, multiplexer_17_out, sub_1_s;

  Comparator #(.Bits(5)) comparator_1 (.a(State), .b({5{1'b1}}), .eq(comparator_1_eq));  // open: gt, lt
  LookUpTable lookuptable_1 (
    .in0(State[0]), .in1(State[1]), .in2(State[2]), .in3(State[3]), .in4(State[4]), .out(lookuptable_1_out));
  Comparator #(.Bits(5)) comparator_2 (.a(State), .b(5'b11100), .eq(comparator_2_eq));  // open: gt, lt
  Comparator #(.Bits(5)) comparator_3 (.a(State), .b(5'b11010), .eq(comparator_3_eq));  // open: gt, lt
  Comparator #(.Bits(5)) comparator_4 (.a(State), .b(5'b11001), .eq(comparator_4_eq));  // open: gt, lt
  Comparator #(.Bits(5)) comparator_5 (.a(State), .b(5'b01101), .eq(comparator_5_eq));  // open: gt, lt
  Comparator #(.Bits(5)) comparator_6 (.a(State), .b(5'b01110), .eq(comparator_6_eq));  // open: gt, lt
  Comparator #(.Bits(5)) comparator_7 (.a(State), .b(5'b10001), .eq(comparator_7_eq));  // open: gt, lt
  Comparator #(.Bits(5)) comparator_8 (.a(State), .b(5'b10010), .eq(comparator_8_eq));  // open: gt, lt
  or or_1 (or_1_out, lookuptable_1_out, or_2_out);
  Multiplexer #(.Bits(2)) multiplexer_1 (.sel(comparator_2_eq), .in_0(2'b00), .in_1(2'b01), .out(multiplexer_1_out));
  Multiplexer #(.Bits(2)) multiplexer_2 (.sel(comparator_3_eq), .in_0(2'b00), .in_1(2'b01), .out(multiplexer_2_out));
  Multiplexer #(.Bits(2)) multiplexer_3 (.sel(comparator_4_eq), .in_0(2'b00), .in_1(2'b01), .out(multiplexer_3_out));
  or or_2 (or_2_out, comparator_1_eq, reset);
  Add #(.Bits(2)) add_1 (.a(Change5), .b(multiplexer_1_out), .c_i(1'b0), .s(add_1_s));  // open: c_o
  Add #(.Bits(2)) add_2 (.a(Change10), .b(multiplexer_2_out), .c_i(1'b0), .s(add_2_s));  // open: c_o
  Add #(.Bits(2)) add_3 (.a(Change20), .b(multiplexer_3_out), .c_i(1'b0), .s(add_3_s));  // open: c_o
  Multiplexer multiplexer_4 (.sel(comparator_5_eq), .in_0(CoffeeOut), .in_1(1'b1), .out(multiplexer_4_out));
  Multiplexer multiplexer_5 (.sel(comparator_6_eq), .in_0(TeaOut), .in_1(1'b1), .out(multiplexer_5_out));
  or or_3 (or_3_out, comparator_7_eq, reset, comparator_8_eq);
  and and_1 (and_1_out, ~clock, or_1_out);  // And
  Multiplexer #(.Bits(2)) multiplexer_6 (.sel(or_2_out), .in_0(add_1_s), .in_1(2'b00), .out(multiplexer_6_out));
  Multiplexer #(.Bits(2)) multiplexer_7 (.sel(or_2_out), .in_0(add_2_s), .in_1(2'b00), .out(multiplexer_7_out));
  Multiplexer #(.Bits(2)) multiplexer_8 (.sel(or_2_out), .in_0(add_3_s), .in_1(2'b00), .out(multiplexer_8_out));
  Multiplexer multiplexer_9 (.sel(or_3_out), .in_0(multiplexer_4_out), .in_1(1'b0), .out(multiplexer_9_out));
  Multiplexer multiplexer_10 (.sel(or_3_out), .in_0(multiplexer_5_out), .in_1(1'b0), .out(multiplexer_10_out));
  D_FF #(.Bits(2)) d_ff_1 (.D(multiplexer_6_out), .C(and_1_out), .Q(Change5));  // open: nQ
  D_FF #(.Bits(2)) d_ff_2 (.D(multiplexer_7_out), .C(and_1_out), .Q(Change10));  // open: nQ
  D_FF #(.Bits(2)) d_ff_3 (.D(multiplexer_8_out), .C(and_1_out), .Q(Change20));  // open: nQ
  D_FF d_ff_4 (.D(multiplexer_9_out), .C(clock), .Q(CoffeeOut));  // open: nQ
  D_FF d_ff_5 (.D(multiplexer_10_out), .C(clock), .Q(TeaOut));  // open: nQ
  Comparator #(.Bits(5)) comparator_9 (.a(State), .b(5'b01101), .eq(comparator_9_eq));  // open: gt, lt
  Comparator #(.Bits(5)) comparator_10 (.a(State), .b(5'b01110), .eq(comparator_10_eq));  // open: gt, lt
  // Probe on State
  not not_1 (not_1_out, State[3]);
  Multiplexer #(.Selector_Bits(3), .Bits(6)) multiplexer_11 (
    .sel(State[2:0]), .in_0({6{1'b0}}), .in_1(6'b010100), .in_2(6'b001010), .in_3({6{1'b0}}),
    .in_4(6'b000101), .in_5(6'b011001), .in_6(6'b010100), .in_7({6{1'b0}}), .out(multiplexer_11_out));
  Add #(.Bits(6)) add_4 (.a(Balance), .b(multiplexer_12_out), .c_i(1'b0), .s(add_4_s));  // open: c_o
  Sub #(.Bits(6)) sub_1 (.a(Balance), .b(multiplexer_12_out), .c_i(1'b0), .s(sub_1_s));  // open: c_o
  Multiplexer #(.Bits(6)) multiplexer_12 (
    .sel(not_1_out), .in_0(multiplexer_11_out), .in_1({6{1'b0}}), .out(multiplexer_12_out));
  Comparator #(.Bits(6)) comparator_11 (.a(Balance), .b(6'b101110), .lt(comparator_11_lt));  // open: gt, eq
  Comparator #(.Bits(6)) comparator_12 (.a(Balance), .b(6'b011000), .gt(comparator_12_gt));  // open: eq, lt
  or or_4 (or_4_out, State[4], comparator_9_eq, comparator_10_eq);
  Multiplexer #(.Bits(5)) multiplexer_13 (.sel(and_2_out), .in_0(5'b01000), .in_1(5'b01100), .out(multiplexer_13_out));
  and and_2 (and_2_out, P5_t, comparator_11_lt);
  Multiplexer #(.Bits(5)) multiplexer_14 (
    .sel(and_3_out), .in_0(multiplexer_25_out), .in_1(5'b01101), .out(multiplexer_14_out));
  and and_3 (and_3_out, comparator_12_gt, Pcoffee_t);
  Comparator #(.Bits(6)) comparator_13 (.a(Balance), .b(6'b000100), .gt(comparator_13_gt));  // open: eq, lt
  Multiplexer #(.Bits(6)) multiplexer_15 (.sel(or_4_out), .in_0(add_4_s), .in_1(sub_1_s), .out(multiplexer_15_out));
  Multiplexer #(.Bits(5)) multiplexer_16 (
    .sel(comparator_13_gt), .in_0(5'b01000), .in_1(5'b11100), .out(multiplexer_16_out));
  LookUpTable lookuptable_2 (
    .in0(State[0]), .in1(State[1]), .in2(State[2]), .in3(State[3]), .in4(State[4]), .out(lookuptable_2_out));
  Multiplexer #(.Bits(6)) multiplexer_17 (
    .sel(reset), .in_0(multiplexer_15_out), .in_1({6{1'b0}}), .out(multiplexer_17_out));
  or or_5 (or_5_out, reset, lookuptable_2_out);
  Comparator #(.Bits(6)) comparator_14 (.a(Balance), .b(6'b101001), .lt(comparator_14_lt));  // open: gt, eq
  Comparator #(.Bits(6)) comparator_15 (.a(Balance), .b(6'b010011), .gt(comparator_15_gt));  // open: eq, lt
  Comparator #(.Bits(6)) comparator_16 (.a(Balance), .b(6'b001001), .gt(comparator_16_gt));  // open: eq, lt
  D_FF #(.Bits(6)) d_ff_6 (.D(multiplexer_17_out), .C(and_5_out), .Q(Balance));  // open: nQ
  Multiplexer #(.Bits(5)) multiplexer_18 (
    .sel(and_4_out), .in_0(multiplexer_13_out), .in_1(5'b01010), .out(multiplexer_18_out));
  and and_4 (and_4_out, P10_t, comparator_14_lt);
  Multiplexer #(.Bits(5)) multiplexer_19 (
    .sel(and_6_out), .in_0(multiplexer_14_out), .in_1(5'b01110), .out(multiplexer_19_out));
  Multiplexer #(.Bits(5)) multiplexer_20 (.sel(Pnext_t), .in_0(5'b10000), .in_1(5'b10001), .out(multiplexer_20_out));
  Multiplexer #(.Bits(5)) multiplexer_21 (
    .sel(comparator_16_gt), .in_0(multiplexer_16_out), .in_1(5'b11010), .out(multiplexer_21_out));
  and and_5 (and_5_out, clock, or_5_out);
  and and_6 (and_6_out, comparator_15_gt, Ptea_t);
  Comparator #(.Bits(6)) comparator_17 (.a(Balance), .b(6'b010011), .gt(comparator_17_gt));  // open: eq, lt
  Multiplexer #(.Bits(5)) multiplexer_22 (
    .sel(Pchange_t), .in_0(multiplexer_19_out), .in_1({5{1'b1}}), .out(multiplexer_22_out));
  Multiplexer #(.Bits(5)) multiplexer_23 (
    .sel(Pchange_t), .in_0(multiplexer_20_out), .in_1(5'b10010), .out(multiplexer_23_out));
  Multiplexer #(.Bits(5)) multiplexer_24 (
    .sel(comparator_17_gt), .in_0(multiplexer_21_out), .in_1(5'b11001), .out(multiplexer_24_out));
  Comparator #(.Bits(6)) comparator_18 (.a(Balance), .b(6'b011111), .lt(comparator_18_lt));  // open: gt, eq
  Multiplexer #(.Bits(5)) multiplexer_25 (
    .sel(and_14_out), .in_0(multiplexer_18_out), .in_1(5'b01001), .out(multiplexer_25_out));
  Multiplexer #(.Bits(5)) multiplexer_26 (
    .sel(reset), .in_0(multiplexer_22_out), .in_1({5{1'b0}}), .out(multiplexer_26_out));
  Multiplexer #(.Bits(5)) multiplexer_27 (
    .sel(reset), .in_0(multiplexer_23_out), .in_1({5{1'b0}}), .out(multiplexer_27_out));
  Multiplexer #(.Bits(5)) multiplexer_28 (
    .sel(reset), .in_0(multiplexer_24_out), .in_1({5{1'b0}}), .out(multiplexer_28_out));
  and and_7 (and_7_out, Pcoffee, ~reset);  // And
  and and_8 (and_8_out, Ptea, ~reset);  // And
  and and_9 (and_9_out, Pchange, ~reset);  // And
  and and_10 (and_10_out, Pnext, ~reset);  // And
  and and_11 (and_11_out, P5, ~reset);  // And
  and and_12 (and_12_out, P10, ~reset);  // And
  and and_13 (and_13_out, P20, ~reset);  // And
  and and_14 (and_14_out, P20_t, comparator_18_lt);
  D_FF d_ff_7 (.D(and_7_out), .C(clock), .nQ(d_ff_7_nq));  // open: Q
  D_FF d_ff_8 (.D(and_8_out), .C(clock), .nQ(d_ff_8_nq));  // open: Q
  D_FF d_ff_9 (.D(and_9_out), .C(clock), .nQ(d_ff_9_nq));  // open: Q
  D_FF d_ff_10 (.D(and_10_out), .C(clock), .nQ(d_ff_10_nq));  // open: Q
  D_FF d_ff_11 (.D(and_11_out), .C(clock), .nQ(d_ff_11_nq));  // open: Q
  D_FF d_ff_12 (.D(and_12_out), .C(clock), .nQ(d_ff_12_nq));  // open: Q
  D_FF d_ff_13 (.D(and_13_out), .C(clock), .nQ(d_ff_13_nq));  // open: Q
  and and_15 (and_15_out, and_7_out, d_ff_7_nq);
  and and_16 (and_16_out, and_8_out, d_ff_8_nq);
  and and_17 (and_17_out, and_9_out, d_ff_9_nq);
  and and_18 (and_18_out, and_10_out, d_ff_10_nq);
  and and_19 (and_19_out, and_11_out, d_ff_11_nq);
  and and_20 (and_20_out, and_12_out, d_ff_12_nq);
  and and_21 (and_21_out, and_13_out, d_ff_13_nq);
  Multiplexer #(.Selector_Bits(5), .Bits(5)) multiplexer_29 (
    .sel(State), .in_0(5'b01000), .in_1({5{1'b0}}), .in_2({5{1'b0}}), .in_3({5{1'b0}}), .in_4({5{1'b0}}),
    .in_5({5{1'b0}}), .in_6({5{1'b0}}), .in_7({5{1'b0}}), .in_8(multiplexer_26_out), .in_9(5'b01000),
    .in_10(5'b01000), .in_11({5{1'b0}}), .in_12(5'b01000), .in_13(5'b10000), .in_14(5'b10000),
    .in_15({5{1'b0}}), .in_16(multiplexer_27_out), .in_17(5'b01000), .in_18({5{1'b1}}), .in_19({5{1'b0}}),
    .in_20({5{1'b0}}), .in_21({5{1'b0}}), .in_22({5{1'b0}}), .in_23({5{1'b0}}), .in_24(multiplexer_28_out),
    .in_25(5'b11000), .in_26(5'b11000), .in_27({5{1'b0}}), .in_28(5'b11000), .in_29({5{1'b0}}),
    .in_30({5{1'b0}}), .in_31(5'b11000), .out(multiplexer_29_out));
  D_FF d_ff_14 (.D(and_15_out), .C(clock), .Q(Pcoffee_t));  // open: nQ
  D_FF d_ff_15 (.D(and_16_out), .C(clock), .Q(Ptea_t));  // open: nQ
  D_FF d_ff_16 (.D(and_17_out), .C(clock), .Q(Pchange_t));  // open: nQ
  D_FF d_ff_17 (.D(and_18_out), .C(clock), .Q(Pnext_t));  // open: nQ
  D_FF d_ff_18 (.D(and_19_out), .C(clock), .Q(P5_t));  // open: nQ
  D_FF d_ff_19 (.D(and_20_out), .C(clock), .Q(P10_t));  // open: nQ
  D_FF d_ff_20 (.D(and_21_out), .C(clock), .Q(P20_t));  // open: nQ
  D_FF #(.Bits(5)) u_State (.D(multiplexer_29_out), .C(clock), .Q(State));  // open: nQ

  // Other names for the same wires on the sheet: Clk = clock

  // Notes on the sheet:
  //   contents of lookuptable_1 (hex, n*v repeats v):
  //   9*0,a,64,0,a,a,64,10*0,1,1,0,1,0,0,a
  //   contents of lookuptable_2 (hex, n*v repeats v):
  //   4*0,a,0,0,0,1,1,1,0,b,1,1,10*0,1,1,0,1
  //   5
endmodule

/* Test case T1:
clock reset P5 P10 P20 Pcoffee Ptea Pchange Pnext Balance CoffeeOut TeaOut Change5 Change10 Change20
0 1 0 0 0 0 0 0 0 x x x x x x
1 1 0 0 0 0 0 0 0 0 0 0 0 0 0
0 0 0 0 0 1 0 0 0 0 0 0 0 0 0
1 0 0 0 0 1 0 0 0 0 0 0 0 0 0
0 0 0 0 0 0 0 0 0 x x x x x x
1 0 0 0 0 0 0 0 0 x x x x x x
0 0 0 0 0 0 0 0 0 x x x x x x
1 0 0 0 0 0 0 0 0 x x x x x x
0 0 0 0 0 0 0 0 0 x x x x x x
1 0 0 0 0 0 0 0 0 x x x x x x
0 0 0 0 0 0 0 0 0 x x x x x x
1 0 0 0 0 0 0 0 0 x x x x x x
0 0 0 0 0 0 0 0 0 x x x x x x
1 0 0 0 0 0 0 0 0 x x x x x x
0 0 0 0 0 0 0 0 0 x x x x x x
1 0 0 0 0 0 0 0 0 x x x x x x
0 0 0 0 0 0 0 0 0 x x x x x x
1 0 0 0 0 0 0 0 0 x x x x x x
0 0 0 0 0 0 0 0 0 x x x x x x
1 0 0 0 0 0 0 0 0 x x x x x x
0 0 0 0 0 0 0 0 0 x x x x x x
1 0 0 0 0 0 0 0 0 x x x x x x
0 0 0 0 0 0 0 0 0 x x x x x x
1 0 0 0 0 0 0 0 0 x x x x x x
0 0 0 0 0 0 0 0 0 x x x x x x
1 0 0 0 0 0 0 0 0 x x x x x x
0 0 0 0 0 0 0 0 0 x x x x x x
1 0 0 0 0 0 0 0 0 x x x x x x
0 0 0 0 0 0 0 0 0 x x x x x x
1 0 0 0 0 0 0 0 0 x x x x x x
0 0 0 0 0 0 0 0 0 x x x x x x
1 0 0 0 0 0 0 0 0 x x x x x x
0 0 0 0 0 0 0 0 0 x x x x x x
1 0 0 0 0 0 0 0 0 x x x x x x
0 0 0 0 0 0 0 0 0 x x x x x x
1 0 0 0 0 0 0 0 0 x x x x x x
0 0 0 0 0 0 0 0 0 x x x x x x
1 0 0 0 0 0 0 0 0 x x x x x x
0 0 0 0 0 0 0 0 0 x x x x x x
1 0 0 0 0 0 0 0 0 x x x x x x
0 0 0 0 0 0 0 0 0 x x x x x x
1 0 0 0 0 0 0 0 0 x x x x x x
0 0 0 0 0 0 0 0 0 x x x x x x
1 0 0 0 0 0 0 0 0 x x x x x x
0 0 0 0 0 0 0 0 0 0 0 0 0 0 0
1 0 0 0 0 0 0 0 0 0 0 0 0 0 0
0 0 0 0 0 0 1 0 0 0 0 0 0 0 0
1 0 0 0 0 0 1 0 0 0 0 0 0 0 0
0 0 0 0 0 0 0 0 0 x x x x x x
1 0 0 0 0 0 0 0 0 x x x x x x
0 0 0 0 0 0 0 0 0 x x x x x x
1 0 0 0 0 0 0 0 0 x x x x x x
0 0 0 0 0 0 0 0 0 x x x x x x
1 0 0 0 0 0 0 0 0 x x x x x x
0 0 0 0 0 0 0 0 0 x x x x x x
1 0 0 0 0 0 0 0 0 x x x x x x
0 0 0 0 0 0 0 0 0 x x x x x x
1 0 0 0 0 0 0 0 0 x x x x x x
0 0 0 0 0 0 0 0 0 x x x x x x
1 0 0 0 0 0 0 0 0 x x x x x x
0 0 0 0 0 0 0 0 0 x x x x x x
1 0 0 0 0 0 0 0 0 x x x x x x
0 0 0 0 0 0 0 0 0 x x x x x x
1 0 0 0 0 0 0 0 0 x x x x x x
0 0 0 0 0 0 0 0 0 x x x x x x
1 0 0 0 0 0 0 0 0 x x x x x x
0 0 0 0 0 0 0 0 0 x x x x x x
1 0 0 0 0 0 0 0 0 x x x x x x
0 0 0 0 0 0 0 0 0 x x x x x x
1 0 0 0 0 0 0 0 0 x x x x x x
0 0 0 0 0 0 0 0 0 x x x x x x
1 0 0 0 0 0 0 0 0 x x x x x x
0 0 0 0 0 0 0 0 0 x x x x x x
1 0 0 0 0 0 0 0 0 x x x x x x
0 0 0 0 0 0 0 0 0 x x x x x x
1 0 0 0 0 0 0 0 0 x x x x x x
0 0 0 0 0 0 0 0 0 x x x x x x
1 0 0 0 0 0 0 0 0 x x x x x x
0 0 0 0 0 0 0 0 0 x x x x x x
1 0 0 0 0 0 0 0 0 x x x x x x
0 0 0 0 0 0 0 0 0 x x x x x x
1 0 0 0 0 0 0 0 0 x x x x x x
0 0 0 0 0 0 0 0 0 x x x x x x
1 0 0 0 0 0 0 0 0 x x x x x x
0 0 0 0 0 0 0 0 0 x x x x x x
1 0 0 0 0 0 0 0 0 x x x x x x
0 0 0 0 0 0 0 0 0 x x x x x x
1 0 0 0 0 0 0 0 0 x x x x x x
0 0 0 0 0 0 0 0 0 0 0 0 0 0 0
1 0 0 0 0 0 0 0 0 0 0 0 0 0 0
0 0 0 0 1 0 0 0 0 0 0 0 0 0 0
1 0 0 0 1 0 0 0 0 0 0 0 0 0 0
0 0 0 0 0 0 0 0 0 x x x x x x
1 0 0 0 0 0 0 0 0 x x x x x x
0 0 0 0 0 0 0 0 0 x x x x x x
1 0 0 0 0 0 0 0 0 x x x x x x
0 0 0 0 0 0 0 0 0 x x x x x x
1 0 0 0 0 0 0 0 0 x x x x x x
0 0 0 0 0 0 0 0 0 x x x x x x
1 0 0 0 0 0 0 0 0 x x x x x x
0 0 0 0 0 0 0 0 0 x x x x x x
1 0 0 0 0 0 0 0 0 x x x x x x
0 0 0 0 0 0 0 0 0 x x x x x x
1 0 0 0 0 0 0 0 0 x x x x x x
0 0 0 0 0 0 0 0 0 x x x x x x
1 0 0 0 0 0 0 0 0 x x x x x x
0 0 0 0 0 0 0 0 0 x x x x x x
1 0 0 0 0 0 0 0 0 x x x x x x
0 0 0 0 0 0 0 0 0 x x x x x x
1 0 0 0 0 0 0 0 0 x x x x x x
0 0 0 0 0 0 0 0 0 x x x x x x
1 0 0 0 0 0 0 0 0 x x x x x x
0 0 0 0 0 0 0 0 0 x x x x x x
1 0 0 0 0 0 0 0 0 x x x x x x
0 0 0 0 0 0 0 0 0 x x x x x x
1 0 0 0 0 0 0 0 0 x x x x x x
0 0 0 0 0 0 0 0 0 x x x x x x
1 0 0 0 0 0 0 0 0 x x x x x x
0 0 0 0 0 0 0 0 0 x x x x x x
1 0 0 0 0 0 0 0 0 x x x x x x
0 0 0 0 0 0 0 0 0 x x x x x x
1 0 0 0 0 0 0 0 0 x x x x x x
0 0 0 0 0 0 0 0 0 x x x x x x
1 0 0 0 0 0 0 0 0 x x x x x x
0 0 0 0 0 0 0 0 0 x x x x x x
1 0 0 0 0 0 0 0 0 x x x x x x
0 0 0 0 0 0 0 0 0 x x x x x x
1 0 0 0 0 0 0 0 0 x x x x x x
0 0 0 0 0 0 0 0 0 x x x x x x
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*/
