// Digital circuit main.dig as structural Verilog
module main (
  input  [8:0] N,
  input  reset,
  input  start,
  input  clock,
  output done,
  output [7:0] displayout,
  output [15:0] clockcount,
  output valid
);

  wire and_1_out, and_2_out, comparator_1_gt, comparator_2_lt, comparator_3_lt, comparator_4_lt, s0, s0_t,
       s1, s1_t, s2, s2_t, s3, s3_t, s4, s4_t, s5, s5_t, s6, s6_t, s7, s7_t;
  wire [2:0] multiplexer_1_out, multiplexer_3_out, multiplexer_4_out, next1, next3, state, state_t;
  wire [7:0] cntreg, cntreg_t, multiplexer_10_out, multiplexer_16_out, RAM, ROM;
  wire [8:0] add_1_s, add_2_s, add_3_s, cnt, i, i_t, idx, idx_t, multiplexer_11_out, N_t, ramreg, ramreg_t,
       romreg, romreg_t, sub_1_s, sub_2_s;

  Comparator #(.Bits(9)) comparator_1 (.a(cnt), .b({9{1'b0}}), .gt(comparator_1_gt));  // open: eq, lt
  Comparator #(.Bits(9)) comparator_2 (.a(idx_t), .b(9'h100), .lt(comparator_2_lt));  // open: gt, eq
  Comparator #(.Bits(9)) comparator_3 (.a(i_t), .b(N_t), .lt(comparator_3_lt));  // open: gt, eq
  Multiplexer #(.Bits(3)) multiplexer_1 (.sel(comparator_1_gt), .in_0(3'b101), .in_1(3'b100), .out(multiplexer_1_out));
  and and_1 (and_1_out, comparator_2_lt, comparator_3_lt);
  Multiplexer #(.Bits(3)) multiplexer_2 (.sel(and_1_out), .in_0(3'b110), .in_1(multiplexer_1_out), .out(next3));
  Multiplexer #(.Bits(3)) multiplexer_3 (.sel(start), .in_0(3'b000), .in_1(3'b001), .out(multiplexer_3_out));
  Multiplexer #(.Bits(3)) multiplexer_4 (.sel(reset), .in_0(3'b110), .in_1(3'b000), .out(multiplexer_4_out));
  Demultiplexer #(.Selector_Bits(3)) demultiplexer_1 (
    .sel(state_t), .in(1'b1), .out_0(s0_t), .out_1(s1_t), .out_2(s2_t), .out_3(s3_t), .out_4(s4_t),
    .out_5(s5_t), .out_6(s6_t), .out_7(s7_t));
  Comparator #(.Bits(9)) comparator_4 (.a(i_t), .b(N_t), .lt(comparator_4_lt));  // open: gt, eq
  and and_2 (and_2_out, clock, start);
  Multiplexer #(.Bits(3), .Selector_Bits(3)) multiplexer_5 (
    .sel(state_t), .in_0(multiplexer_3_out), .in_1(next1), .in_2(3'b011), .in_3(next3), .in_4(next3),
    .in_5(next3), .in_6(multiplexer_4_out), .in_7(3'b000), .out(state));
  Multiplexer #(.Bits(3)) multiplexer_6 (.sel(comparator_4_lt), .in_0(3'b010), .in_1(3'b001), .out(next1));
  Demultiplexer #(.Selector_Bits(3)) demultiplexer_2 (
    .sel(state), .in(1'b1), .out_0(s0), .out_1(s1), .out_2(s2), .out_3(s3), .out_4(s4), .out_5(s5),
    .out_6(s6), .out_7(s7));
  D_FF #(.Bits(9)) d_ff_1 (.D(9'h4), .C(and_2_out), .Q(N_t));  // open: nQ
  D_FF #(.Bits(3)) d_ff_2 (.D(state), .C(clock), .Q(state_t));  // open: nQ
  // Probe on N_t
  // Probe on state_t
  Seven_Seg_Hex seven_seg_hex_1 (.d(displayout[7:4]), .dp(1'b0));
  Multiplexer #(.Selector_Bits(3), .Bits(8)) multiplexer_7 (
    .sel(state_t), .in_0(cntreg_t), .in_1(ROM), .in_2(cntreg_t), .in_3(cntreg_t), .in_4(idx[7:0]),
    .in_5(cntreg_t), .in_6(cntreg_t), .in_7(cntreg_t), .out(cntreg));
  Multiplexer #(.Selector_Bits(3), .Bits(9)) multiplexer_8 (
    .sel(state_t), .in_0({9{1'b0}}), .in_1({9{1'b0}}), .in_2({9{1'b0}}), .in_3(i), .in_4(i), .in_5(i),
    .in_6({9{1'b0}}), .in_7({9{1'b0}}), .out(ramreg));
  Seven_Seg_Hex seven_seg_hex_2 (.d(displayout[3:0]), .dp(1'b0));
  Multiplexer #(.Bits(9), .Selector_Bits(3)) multiplexer_9 (
    .sel(state_t), .in_0({9{1'b0}}), .in_1(i_t), .in_2({9{1'b0}}), .in_3({9{1'b0}}), .in_4({9{1'b0}}),
    .in_5({9{1'b0}}), .in_6({9{1'b0}}), .in_7({9{1'b0}}), .out(romreg));
  D_FF #(.Bits(8)) d_ff_3 (.D(cntreg), .C(clock), .Q(cntreg_t));  // open: nQ
  D_FF #(.Bits(9)) d_ff_4 (.D(ramreg), .C(clock), .Q(ramreg_t));  // open: nQ
  D_FF #(.Bits(9)) d_ff_5 (.D(romreg), .C(clock), .Q(romreg_t));  // open: nQ
  // Probe on cntreg_t
  // Probe on ramreg_t
  // Probe on romreg_t
  Add #(.Bits(9)) add_1 (.a(cnt), .b(9'h1), .c_i(1'b0), .s(add_1_s));  // open: c_o
  Sub #(.Bits(9)) sub_1 (.a(cnt), .b(9'h1), .c_i(1'b0), .s(sub_1_s));  // open: c_o
  Multiplexer #(.Selector_Bits(3), .Bits(8)) multiplexer_10 (
    .sel(state_t), .in_0(RAM), .in_1(RAM), .in_2(RAM), .in_3(RAM), .in_4(idx[7:0]), .in_5(RAM), .in_6(RAM),
    .in_7(RAM), .out(multiplexer_10_out));
  ROM #(.AddrBits(9), .Bits(8)) ROMFILE (.A(romreg_t), .sel(1'b1), .D(ROM));
  Multiplexer #(.Selector_Bits(3), .Bits(9)) multiplexer_11 (
    .sel(state_t), .in_0(cnt), .in_1(add_1_s), .in_2(cnt), .in_3(cnt), .in_4(sub_1_s), .in_5(cnt),
    .in_6(cnt), .in_7(cnt), .out(multiplexer_11_out));
  RAMDualPort #(.AddrBits(9), .Bits(8)) u_RAM (
    .A(ramreg_t), .Din(multiplexer_10_out), .str(1'b1), .C(clock), .ld(1'b1), .D(RAM));
  RAMDualPort #(.AddrBits(8), .Bits(9)) data (
    .A(cntreg_t), .Din(multiplexer_11_out), .str(1'b1), .C(clock), .ld(1'b1), .D(cnt));
  Multiplexer #(.Selector_Bits(3)) multiplexer_12 (
    .sel(state_t), .in_0(1'b0), .in_1(1'b0), .in_2(1'b0), .in_3(1'b0), .in_4(1'b0), .in_5(1'b0), .in_6(1'b1),
    .in_7(1'b0), .out(done));
  Add #(.Bits(9)) add_2 (.a(i_t), .b(9'h1), .c_i(1'b0), .s(add_2_s));  // open: c_o
  Sub #(.Bits(9)) sub_2 (.a(i_t), .b(9'h1), .c_i(1'b0), .s(sub_2_s));  // open: c_o
  Add #(.Bits(9)) add_3 (.a(idx_t), .b(9'h1), .c_i(1'b0), .s(add_3_s));  // open: c_o
  Multiplexer #(.Selector_Bits(3)) multiplexer_13 (
    .sel(state_t), .in_0(1'b0), .in_1(1'b0), .in_2(1'b0), .in_3(1'b0), .in_4(1'b1), .in_5(1'b0), .in_6(1'b0),
    .in_7(1'b0), .out(valid));
  Multiplexer #(.Bits(9), .Selector_Bits(3)) multiplexer_14 (
    .sel(state_t), .in_0({9{1'b0}}), .in_1(add_2_s), .in_2({9{1'b0}}), .in_3(i_t), .in_4(sub_2_s),
    .in_5(i_t), .in_6(i_t), .in_7(i_t), .out(i));
  Multiplexer #(.Selector_Bits(3), .Bits(9)) multiplexer_15 (
    .sel(state_t), .in_0(idx_t), .in_1(idx_t), .in_2({9{1'b0}}), .in_3(idx_t), .in_4(idx_t), .in_5(add_3_s),
    .in_6(idx_t), .in_7(idx_t), .out(idx));
  D_FF #(.Bits(9)) d_ff_6 (.D(i), .C(clock), .Q(i_t));  // open: nQ
  D_FF #(.Bits(9)) d_ff_7 (.D(idx), .C(clock), .Q(idx_t));  // open: nQ
  // Probe on i_t
  // Probe on idx_t
  Multiplexer #(.Selector_Bits(3), .Bits(8)) multiplexer_16 (
    .sel(state_t), .in_0({8{1'b0}}), .in_1({8{1'b0}}), .in_2({8{1'b0}}), .in_3(displayout), .in_4(idx[7:0]),
    .in_5({8{1'b0}}), .in_6({8{1'b0}}), .in_7({8{1'b0}}), .out(multiplexer_16_out));
  D_FF #(.Bits(8)) d_ff_8 (.D(multiplexer_16_out), .C(clock), .Q(displayout));  // open: nQ
  // Probe on displayout

  assign clockcount = {16{1'b0}};

  // Other names for the same wires on the sheet: clk = clock; out[7:0] = displayout

  // Notes on the sheet:
  //   contents of ROMFILE (hex, n*v repeats v):
  //   5,4,3,2
endmodule
