// Digital circuit old.dig as structural Verilog
module old (
  input  [8:0] N,
  input  reset,
  input  start,
  input  clock,
  output done,
  output [7:0] displayout,
  output [15:0] clockcount,
  output valid
);

  wire and_1_out, and_2_out, and_3_out, and_4_out, and_5_out, and_6_out, and_7_out, and_8_out, and_9_out,
       comparator_1_eq, comparator_2_eq, comparator_3_eq, comparator_4_eq, comparator_5_eq, comparator_6_lt,
       comparator_7_gt, flag, multiplexer_12_out, not_1_out, not_2_out, or_1_out, or_2_out, or_3_out,
       or_4_out, or_5_out, or_6_out, or_7_out, or_8_out, s0, s0_t, s1, s1_t, s2, s2_t, s3, s3_t, s4, s4_t,
       s5, s5_t, s6, s6_t, s7, s7_t;
  wire [2:0] multiplexer_1_out, multiplexer_2_out, multiplexer_3_out, multiplexer_4_out, multiplexer_5_out,
       state, state_t;
  wire [7:0] add_2_s, cur, multiplexer_9_out, multiplexer_11_out, ROMFILE_d;
  wire [8:0] add_1_s, add_3_s, add_4_s, cnt, i, multiplexer_6_out, multiplexer_7_out, multiplexer_10_out,
       multiplexer_13_out, N_t, RAM1, sub_1_s;

  Comparator #(.Bits(9)) comparator_1 (.a(i), .b(N_t), .eq(comparator_1_eq));  // open: gt, lt
  Comparator #(.Bits(9)) comparator_2 (.a(cnt), .b(N_t), .eq(comparator_2_eq));  // open: gt, lt
  Multiplexer #(.Bits(3)) multiplexer_1 (.sel(comparator_1_eq), .in_0(3'b010), .in_1(3'b011), .out(multiplexer_1_out));
  Multiplexer #(.Bits(3)) multiplexer_2 (.sel(comparator_2_eq), .in_0(3'b110), .in_1(3'b111), .out(multiplexer_2_out));
  Comparator #(.Bits(9)) comparator_3 (.a(RAM1), .b({9{1'b0}}), .eq(comparator_3_eq));  // open: gt, lt
  Comparator #(.Bits(9)) comparator_4 (.a(cnt), .b(N_t), .eq(comparator_4_eq));  // open: gt, lt
  Add #(.Bits(9)) add_1 (.a(cnt), .b(9'h1), .c_i(1'b0), .s(add_1_s));  // open: c_o
  Multiplexer #(.Bits(3)) multiplexer_3 (.sel(start), .in_0(3'b000), .in_1(3'b001), .out(multiplexer_3_out));
  Multiplexer #(.Bits(3)) multiplexer_4 (.sel(flag), .in_0(3'b101), .in_1(3'b110), .out(multiplexer_4_out));
  Multiplexer #(.Bits(3)) multiplexer_5 (.sel(reset), .in_0(3'b111), .in_1(3'b000), .out(multiplexer_5_out));
  not not_1 (not_1_out, comparator_3_eq);
  or or_1 (or_1_out, s3, s4_t);
  Multiplexer #(.Bits(9)) multiplexer_6 (.sel(comparator_4_eq), .in_0(cnt), .in_1({9{1'b0}}), .out(multiplexer_6_out));
  or or_2 (or_2_out, s3_t, s4_t, s5_t, s6_t);
  Add #(.Bits(8)) add_2 (.a(cur), .b({8{1'b0}}), .c_i(not_1_out), .s(add_2_s));  // open: c_o
  and and_1 (and_1_out, or_1_out, ~clock);  // And
  Multiplexer #(.Bits(9)) multiplexer_7 (
    .sel(or_3_out), .in_0(multiplexer_6_out), .in_1(add_1_s), .out(multiplexer_7_out));
  or or_3 (or_3_out, s5_t, s6_t);
  Comparator #(.Bits(9)) comparator_5 (.a(cnt), .b(N_t), .eq(comparator_5_eq));  // open: gt, lt
  Multiplexer #(.Selector_Bits(3), .Bits(3)) multiplexer_8 (
    .sel(state_t), .in_0(multiplexer_3_out), .in_1(3'b010), .in_2(multiplexer_1_out), .in_3(3'b100),
    .in_4(multiplexer_4_out), .in_5(3'b100), .in_6(multiplexer_2_out), .in_7(multiplexer_5_out), .out(state));
  Multiplexer #(.Bits(8)) multiplexer_9 (.sel(s3), .in_0(add_2_s), .in_1({8{1'b0}}), .out(multiplexer_9_out));
  and and_2 (and_2_out, or_2_out, ~clock);  // And
  and and_3 (and_3_out, s4_t, ~clock);  // And
  D_FF #(.Bits(8)) d_ff_1 (.D(multiplexer_9_out), .C(and_1_out), .Q(cur));  // open: nQ
  Multiplexer #(.Bits(9)) multiplexer_10 (
    .sel(s3_t), .in_0(multiplexer_7_out), .in_1({9{1'b0}}), .out(multiplexer_10_out));
  D_FF d_ff_2 (.D(comparator_5_eq), .C(and_3_out), .Q(flag));  // open: nQ
  D_FF #(.Bits(3)) d_ff_3 (.D(state), .C(clock), .Q(state_t));  // open: nQ
  D_FF #(.Bits(9)) d_ff_4 (.D(multiplexer_10_out), .C(and_2_out), .Q(cnt));  // open: nQ
  // Probe on flag
  // Probe on state_t
  // Probe on state
  // Probe on cur
  // Probe on cnt
  or or_4 (or_4_out, s6, s7);
  Demultiplexer #(.Selector_Bits(3)) demultiplexer_1 (
    .sel(state_t), .in(1'b1), .out_0(s0_t), .out_1(s1_t), .out_2(s2_t), .out_3(s3_t), .out_4(s4_t),
    .out_5(s5_t), .out_6(s6_t), .out_7(s7_t));
  Add #(.Bits(9)) add_3 (.a(i), .b(9'h1), .c_i(1'b0), .s(add_3_s));  // open: c_o
  or or_5 (or_5_out, s4_t, s6_t);
  and and_4 (and_4_out, or_4_out, clock);
  Seven_Seg_Hex seven_seg_hex_1 (.d(displayout[7:4]), .dp(1'b0));
  Demultiplexer #(.Selector_Bits(3)) demultiplexer_2 (
    .sel(state), .in(1'b1), .out_0(s0), .out_1(s1), .out_2(s2), .out_3(s3), .out_4(s4), .out_5(s5),
    .out_6(s6), .out_7(s7));
  and and_5 (and_5_out, s2_t, ~clock);  // And
  and and_6 (and_6_out, or_5_out, clock);
  D_FF d_ff_5 (.D(s6), .C(and_4_out), .Q(valid));  // open: nQ
  Seven_Seg_Hex seven_seg_hex_2 (.d(displayout[3:0]), .dp(1'b0));
  D_FF #(.Bits(9)) d_ff_6 (.D(add_3_s), .C(and_5_out), .Q(i));  // open: nQ
  // Probe on valid
  RAMDualPort #(.AddrBits(9), .Bits(8)) RAM (
    .A(cnt), .Din(RAM1[7:0]), .str(s4_t), .C(and_6_out), .ld(1'b1), .D(displayout));
  // Probe on i
  ROM #(.AddrBits(9), .Bits(8)) ROMFILE (.A(i), .sel(1'b1), .D(ROMFILE_d));
  Comparator #(.Bits(9)) comparator_6 (.a(i), .b(N_t), .lt(comparator_6_lt));  // open: gt, eq
  Comparator #(.Bits(9)) comparator_7 (.a(RAM1), .b({9{1'b0}}), .gt(comparator_7_gt));  // open: eq, lt
  or or_6 (or_6_out, s6, s7);
  // Probe on ROMFILE_d
  Multiplexer #(.Bits(8)) multiplexer_11 (.sel(s2_t), .in_0(cur), .in_1(ROMFILE_d), .out(multiplexer_11_out));
  or or_7 (or_7_out, s2_t, s4, s5);
  and and_7 (and_7_out, or_6_out, clock);
  Multiplexer multiplexer_12 (
    .sel(not_2_out), .in_0(comparator_6_lt), .in_1(comparator_7_gt), .out(multiplexer_12_out));
  not not_2 (not_2_out, s2_t);
  and and_8 (and_8_out, or_7_out, clock);
  D_FF d_ff_7 (.D(s7), .C(and_7_out), .Q(done));  // open: nQ
  and and_9 (and_9_out, clock, start);
  RAMDualPort #(.AddrBits(8), .Bits(9)) data (
    .A(multiplexer_11_out), .Din(multiplexer_13_out), .str(multiplexer_12_out), .C(and_8_out), .ld(1'b1),
    .D(RAM1));
  // Probe on done
  D_FF #(.Bits(9)) d_ff_8 (.D(9'h4), .C(and_9_out), .Q(N_t));  // open: nQ
  // Probe on cur
  // Probe on cnt
  // Probe on RAM1
  // Probe on N_t
  Add #(.Bits(9)) add_4 (.a(RAM1), .b(9'h1), .c_i(1'b0), .s(add_4_s));  // open: c_o
  Sub #(.Bits(9)) sub_1 (.a(RAM1), .b(9'h1), .c_i(1'b0), .s(sub_1_s));  // open: c_o
  // Probe on state_t
  // Probe on state
  Multiplexer #(.Bits(9)) multiplexer_13 (.sel(or_8_out), .in_0(add_4_s), .in_1(sub_1_s), .out(multiplexer_13_out));
  or or_8 (or_8_out, s4_t, s5_t);

  assign clockcount = {16{1'b0}};

  // Other names for the same wires on the sheet: clk = clock; out[7:0] = displayout

  // Notes on the sheet:
  //   contents of ROMFILE (hex, n*v repeats v):
  //   5,4,3,2
  //   Access ram1[j] when state!=2
  //   Otherwise, accecss ram1[rom[i]]
endmodule
