// Digital circuit tawan.dig as structural Verilog
module tawan (
  input  [15:0] A,
  input  \input ,
  input  clk,
  input  reset,
  output [15:0] peak
);

  wire and_1_out, comparator_1_eq, comparator_2_eq, comparator_3_gt, comparator_4_gt, comparator_5_eq,
       comparator_6_gt, comparator_7_eq, comparator_8_gt;
  wire [1:0] multiplexer_1_out, multiplexer_2_out, multiplexer_3_out, multiplexer_7_out, state, state_t;
  wire [15:0] absL, absR, B, B_t, C, C_t, max, multiplexer_5_out, multiplexer_9_out, multiplexer_14_out,
       multiplexer_16_out, sub_1_s, sub_2_s, sub_3_s, sub_4_s, val;
  wire [31:0] add_1_s, counter, counter_t, multiplexer_12_out;

  Multiplexer #(.Bits(2)) multiplexer_1 (.sel(\input ), .in_0(2'b01), .in_1(2'b10), .out(multiplexer_1_out));
  Multiplexer #(.Bits(2)) multiplexer_2 (.sel(\input ), .in_0(2'b01), .in_1(2'b11), .out(multiplexer_2_out));
  Multiplexer #(.Bits(2)) multiplexer_3 (.sel(\input ), .in_0(2'b01), .in_1(2'b11), .out(multiplexer_3_out));
  Multiplexer #(.Selector_Bits(2), .Bits(2)) multiplexer_4 (
    .sel(state_t), .in_0(2'b01), .in_1(multiplexer_1_out), .in_2(multiplexer_2_out),
    .in_3(multiplexer_3_out), .out(state));
  Multiplexer #(.Bits(16)) multiplexer_5 (.sel(reset), .in_0(C), .in_1({16{1'b0}}), .out(multiplexer_5_out));
  D_FF #(.Bits(16)) u_C (.D(multiplexer_5_out), .C(clk), .Q(C_t));  // open: nQ
  Multiplexer #(.Bits(16)) multiplexer_6 (.sel(comparator_1_eq), .in_0(C_t), .in_1(B_t), .out(C));
  Comparator #(.Bits(2)) comparator_1 (.a(2'b10), .b(state), .eq(comparator_1_eq));  // open: gt, lt
  Multiplexer #(.Bits(2)) multiplexer_7 (.sel(reset), .in_0(state), .in_1(2'b01), .out(multiplexer_7_out));
  // Probe on C_t
  Multiplexer #(.Bits(16)) multiplexer_8 (.sel(comparator_2_eq), .in_0(B_t), .in_1(A), .out(B));
  Comparator #(.Bits(2)) comparator_2 (.a(2'b10), .b(state), .eq(comparator_2_eq));  // open: gt, lt
  D_FF #(.Bits(2), .Default(1)) u_state (.D(multiplexer_7_out), .C(clk), .Q(state_t));  // open: nQ
  Multiplexer #(.Bits(16)) multiplexer_9 (.sel(reset), .in_0(B), .in_1({16{1'b0}}), .out(multiplexer_9_out));
  // Probe on state_t
  D_FF #(.Bits(16)) u_B (.D(multiplexer_9_out), .C(clk), .Q(B_t));  // open: nQ
  // Probe on B_t
  Sub #(.Bits(16)) sub_1 (.a(B_t), .b(C_t), .c_i(1'b0), .s(sub_1_s));  // open: c_o
  Sub #(.Bits(16)) sub_2 (.a(C_t), .b(B_t), .c_i(1'b0), .s(sub_2_s));  // open: c_o
  Sub #(.Bits(16)) sub_3 (.a(A), .b(B_t), .c_i(1'b0), .s(sub_3_s));  // open: c_o
  Sub #(.Bits(16)) sub_4 (.a(B_t), .b(A), .c_i(1'b0), .s(sub_4_s));  // open: c_o
  Add #(.Bits(32)) add_1 (.a(counter_t), .b(32'h1), .c_i(1'b0), .s(add_1_s));  // open: c_o
  Add #(.Bits(16)) add_2 (.a(absL), .b(absR), .c_i(1'b0), .s(val));  // open: c_o
  Multiplexer #(.Bits(16)) multiplexer_10 (.sel(comparator_3_gt), .in_0(sub_1_s), .in_1(sub_2_s), .out(absL));
  Multiplexer #(.Bits(16)) multiplexer_11 (.sel(comparator_4_gt), .in_0(sub_3_s), .in_1(sub_4_s), .out(absR));
  Multiplexer #(.Bits(32)) multiplexer_12 (
    .sel(comparator_5_eq), .in_0(counter_t), .in_1(add_1_s), .out(multiplexer_12_out));
  // Probe on val
  // Probe on absL
  Comparator #(.Signed("true"), .Bits(16)) comparator_3 (.a(C_t), .b(B_t), .gt(comparator_3_gt));  // open: eq, lt
  // Probe on absR
  Comparator #(.Signed("true"), .Bits(16)) comparator_4 (.a(B_t), .b(A), .gt(comparator_4_gt));  // open: eq, lt
  Comparator #(.Bits(2)) comparator_5 (.a(2'b10), .b(state), .eq(comparator_5_eq));  // open: gt, lt
  Multiplexer #(.Bits(32)) multiplexer_13 (.sel(reset), .in_0(multiplexer_12_out), .in_1({32{1'b0}}), .out(counter));
  Multiplexer #(.Bits(16)) multiplexer_14 (.sel(comparator_6_gt), .in_0(peak), .in_1(val), .out(multiplexer_14_out));
  Comparator #(.Bits(16)) comparator_6 (.a(val), .b(peak), .gt(comparator_6_gt));  // open: eq, lt
  // Probe on val
  // Probe on peak
  D_FF #(.Bits(32)) u_counter (.D(counter), .C(clk), .Q(counter_t));  // open: nQ
  Multiplexer #(.Bits(16)) multiplexer_15 (.sel(and_1_out), .in_0(peak), .in_1(multiplexer_14_out), .out(max));
  and and_1 (and_1_out, comparator_7_eq, comparator_8_gt);
  Comparator #(.Bits(2)) comparator_7 (.a(state), .b(2'b10), .eq(comparator_7_eq));  // open: gt, lt
  // Probe on counter_t
  Multiplexer #(.Bits(16)) multiplexer_16 (.sel(reset), .in_0(max), .in_1({16{1'b0}}), .out(multiplexer_16_out));
  // Probe on max
  Comparator #(.Bits(32)) comparator_8 (.a(counter), .b(32'h2), .gt(comparator_8_gt));  // open: eq, lt
  D_FF #(.Bits(16)) u_max (.D(multiplexer_16_out), .C(clk), .Q(peak));  // open: nQ

  // Other names for the same wires on the sheet: max_t[15:0] = peak

  // Notes on the sheet:
  //   clk: Hz: 200
  //   we can make reset as a conditional action inside every state
  //   A (directly from input)
endmodule

/* Test case Testcase1:
clk A input reset peak
0 0 0 0 0
1 0 0 0 0
0 0 0 1 0
1 0 0 1 0
0 0  0 0 0
1 0  0 0 0
0 5 1 0 X
1 5 1 0 X
0 0 0 0 X
1 0 0 0 X
0 1 1 0 X
1 1 1 0 X
0 0 0 0 X
1 0 0 0 X
0 0 0 0 X
1 0 0 0 X
0 2 1 0 X
1 2 1 0 X
0 0 0 0 X
1 0 0 0 X
0  0 0 0 5
1  0 0 0 5
0 10 1 0 X
1 10 1 0 X
0 0 0 0 X
1 0 0 0 9
0  0 0 0 9
1  0 0 0 9
0 3 1 0 X
1 3 1 0 X
0 0 0 0 X
1 0 0 0 15
0  0 0 0 15
1  0 0 0 15
0 65526 1 0 X
1 65526 1 0 X
0 0 0 0 X
1 0 0 0 20
0  0 0 0 20
1  0 0 0 20
0 2 1 0 X
1 2 1 0 X
0 0 0 0 X
1 0 0 0 25
0  0 0 0 25
1  0 0 0 25
0 4 1 0 X
1 4 1 0 X
0 0 0 0 X
1 0 0 0 25
0  0 0 0 25
1  0 0 0 25
0 1 1 0 X
1 1 1 0 X
0 0 0 0 X
1 0 0 0 25
0  0 0 0 25
1  0 0 0 25
0 2 1 0 X
1 2 1 0 X
0 0 0 0 X
1 0 0 0 25
*/

/* Test case Testcase3:
clk A input reset peak
0 0 0 0 0
1 0 0 0 0
0 0 0 1 0
1 0 0 1 0
0 0  0 0 0
1 0  0 0 0
0 9924 1 0 X
1 9924 1 0 X
0 0 0 0 X
1 0 0 0 X
0 1714 1 0 X
1 1714 1 0 X
0 0 0 0 X
1 0 0 0 X
0 0 0 0 X
1 0 0 0 X
0 19734 1 0 X
1 19734 1 0 X
0 0 0 0 X
1 0 0 0 X
0  0 0 0 26230
1  0 0 0 26230
0 14144 1 0 X
1 14144 1 0 X
0 0 0 0 X
1 0 0 0 26230
0  0 0 0 26230
1  0 0 0 26230
0 6348 1 0 X
1 6348 1 0 X
0 0 0 0 X
1 0 0 0 26230
0  0 0 0 26230
1  0 0 0 26230
0 29200 1 0 X
1 29200 1 0 X
0 0 0 0 X
1 0 0 0 30648
0  0 0 0 30648
1  0 0 0 30648
0 13658 1 0 X
1 13658 1 0 X
0 0 0 0 X
1 0 0 0 38394
0  0 0 0 38394
1  0 0 0 38394
0 20001 1 0 X
1 20001 1 0 X
0 0 0 0 X
1 0 0 0 38394
0  0 0 0 38394
1  0 0 0 38394
0 23323 1 0 X
1 23323 1 0 X
0 0 0 0 X
1 0 0 0 38394
0  0 0 0 38394
1  0 0 0 38394
0 15516 1 0 X
1 15516 1 0 X
0 0 0 0 X
1 0 0 0 38394
0  0 0 0 38394
1  0 0 0 38394
0 26104 1 0 X
1 26104 1 0 X
0 0 0 0 X
1 0 0 0 38394
0  0 0 0 38394
1  0 0 0 38394
0 23576 1 0 X
1 23576 1 0 X
0 0 0 0 X
1 0 0 0 38394
0  0 0 0 38394
1  0 0 0 38394
0 15152 1 0 X
1 15152 1 0 X
0 0 0 0 X
1 0 0 0 38394
0  0 0 0 38394
1  0 0 0 38394
0 9762 1 0 X
1 9762 1 0 X
0 0 0 0 X
1 0 0 0 38394
0  0 0 0 38394
1  0 0 0 38394
0 3599 1 0 X
1 3599 1 0 X
0 0 0 0 X
1 0 0 0 38394
0  0 0 0 38394
1  0 0 0 38394
0 16576 1 0 X
1 16576 1 0 X
0 0 0 0 X
1 0 0 0 38394
0  0 0 0 38394
1  0 0 0 38394
0 30162 1 0 X
1 30162 1 0 X
0 0 0 0 X
1 0 0 0 38394
0  0 0 0 38394
1  0 0 0 38394
0 30934 1 0 X
1 30934 1 0 X
0 0 0 0 X
1 0 0 0 38394
0  0 0 0 38394
1  0 0 0 38394
0 31029 1 0 X
1 31029 1 0 X
0 0 0 0 X
1 0 0 0 38394
0  0 0 0 38394
1  0 0 0 38394
0 18783 1 0 X
1 18783 1 0 X
0 0 0 0 X
1 0 0 0 38394
0  0 0 0 38394
1  0 0 0 38394
0 1881 1 0 X
1 1881 1 0 X
0 0 0 0 X
1 0 0 0 38394
0  0 0 0 38394
1  0 0 0 38394
0 10695 1 0 X
1 10695 1 0 X
0 0 0 0 X
1 0 0 0 38394
0  0 0 0 38394
1  0 0 0 38394
0 7756 1 0 X
1 7756 1 0 X
0 0 0 0 X
1 0 0 0 38394
0  0 0 0 38394
1  0 0 0 38394
0 14129 1 0 X
1 14129 1 0 X
0 0 0 0 X
1 0 0 0 38394
0  0 0 0 38394
1  0 0 0 38394
0 30596 1 0 X
1 30596 1 0 X
0 0 0 0 X
1 0 0 0 38394
0  0 0 0 38394
1  0 0 0 38394
0 21070 1 0 X
1 21070 1 0 X
0 0 0 0 X
1 0 0 0 38394
0  0 0 0 38394
1  0 0 0 38394
0 15427 1 0 X
1 15427 1 0 X
0 0 0 0 X
1 0 0 0 38394
0  0 0 0 38394
1  0 0 0 38394
0 2565 1 0 X
1 2565 1 0 X
0 0 0 0 X
1 0 0 0 38394
0  0 0 0 38394
1  0 0 0 38394
0 24554 1 0 X
1 24554 1 0 X
0 0 0 0 X
1 0 0 0 38394
0  0 0 0 38394
1  0 0 0 38394
0 25370 1 0 X
1 25370 1 0 X
0 0 0 0 X
1 0 0 0 38394
0  0 0 0 38394
1  0 0 0 38394
0 9273 1 0 X
1 9273 1 0 X
0 0 0 0 X
1 0 0 0 38394
0  0 0 0 38394
1  0 0 0 38394
0 8302 1 0 X
1 8302 1 0 X
0 0 0 0 X
1 0 0 0 38394
0  0 0 0 38394
1  0 0 0 38394
0 3282 1 0 X
1 3282 1 0 X
0 0 0 0 X
1 0 0 0 38394
0  0 0 0 38394
1  0 0 0 38394
0 25633 1 0 X
1 25633 1 0 X
0 0 0 0 X
1 0 0 0 38394
0  0 0 0 38394
1  0 0 0 38394
0 13448 1 0 X
1 13448 1 0 X
0 0 0 0 X
1 0 0 0 38394
0  0 0 0 38394
1  0 0 0 38394
0 5516 1 0 X
1 5516 1 0 X
0 0 0 0 X
1 0 0 0 38394
0  0 0 0 38394
1  0 0 0 38394
0 31976 1 0 X
1 31976 1 0 X
0 0 0 0 X
1 0 0 0 38394
0  0 0 0 38394
1  0 0 0 38394
0 24271 1 0 X
1 24271 1 0 X
0 0 0 0 X
1 0 0 0 38394
0  0 0 0 38394
1  0 0 0 38394
0 6215 1 0 X
1 6215 1 0 X
0 0 0 0 X
1 0 0 0 38394
0  0 0 0 38394
1  0 0 0 38394
0 10282 1 0 X
1 10282 1 0 X
0 0 0 0 X
1 0 0 0 38394
0  0 0 0 38394
1  0 0 0 38394
0 28448 1 0 X
1 28448 1 0 X
0 0 0 0 X
1 0 0 0 38394
0  0 0 0 38394
1  0 0 0 38394
0 19282 1 0 X
1 19282 1 0 X
0 0 0 0 X
1 0 0 0 38394
0  0 0 0 38394
1  0 0 0 38394
0 16410 1 0 X
1 16410 1 0 X
0 0 0 0 X
1 0 0 0 38394
0  0 0 0 38394
1  0 0 0 38394
0 4699 1 0 X
1 4699 1 0 X
0 0 0 0 X
1 0 0 0 38394
0  0 0 0 38394
1  0 0 0 38394
0 17855 1 0 X
1 17855 1 0 X
0 0 0 0 X
1 0 0 0 38394
0  0 0 0 38394
1  0 0 0 38394
0 7295 1 0 X
1 7295 1 0 X
0 0 0 0 X
1 0 0 0 38394
0  0 0 0 38394
1  0 0 0 38394
0 5567 1 0 X
1 5567 1 0 X
0 0 0 0 X
1 0 0 0 38394
0  0 0 0 38394
1  0 0 0 38394
0 5318 1 0 X
1 5318 1 0 X
0 0 0 0 X
1 0 0 0 38394
0  0 0 0 38394
1  0 0 0 38394
0 7523 1 0 X
1 7523 1 0 X
0 0 0 0 X
1 0 0 0 38394
0  0 0 0 38394
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*/

/* Test case Testcase6:
clk A input reset peak
0 0 0 0 0
1 0 0 0 0
0 0 0 1 0
1 0 0 1 0
0 0  0 0 0
1 0  0 0 0
0 64563 1 0 X
1 64563 1 0 X
0 0 0 0 X
1 0 0 0 X
0 64536 1 0 X
1 64536 1 0 X
0 0 0 0 X
1 0 0 0 X
0 0 0 0 X
1 0 0 0 X
0 64709 1 0 X
1 64709 1 0 X
0 0 0 0 X
1 0 0 0 X
0  0 0 0 200
1  0 0 0 200
0 64724 1 0 X
1 64724 1 0 X
0 0 0 0 X
1 0 0 0 200
0  0 0 0 200
1  0 0 0 200
0 64709 1 0 X
1 64709 1 0 X
0 0 0 0 X
1 0 0 0 200
0  0 0 0 200
1  0 0 0 200
0 64804 1 0 X
1 64804 1 0 X
0 0 0 0 X
1 0 0 0 200
0  0 0 0 200
1  0 0 0 200
0 64890 1 0 X
1 64890 1 0 X
0 0 0 0 X
1 0 0 0 200
0  0 0 0 200
1  0 0 0 200
0 64804 1 0 X
1 64804 1 0 X
0 0 0 0 X
1 0 0 0 200
0  0 0 0 200
1  0 0 0 200
0 64917 1 0 X
1 64917 1 0 X
0 0 0 0 X
1 0 0 0 200
0  0 0 0 200
1  0 0 0 200
0 64968 1 0 X
1 64968 1 0 X
0 0 0 0 X
1 0 0 0 200
0  0 0 0 200
1  0 0 0 200
0 64917 1 0 X
1 64917 1 0 X
0 0 0 0 X
1 0 0 0 200
0  0 0 0 200
1  0 0 0 200
0 65085 1 0 X
1 65085 1 0 X
0 0 0 0 X
1 0 0 0 219
0  0 0 0 219
1  0 0 0 219
0 65153 1 0 X
1 65153 1 0 X
0 0 0 0 X
1 0 0 0 236
0  0 0 0 236
1  0 0 0 236
0 65085 1 0 X
1 65085 1 0 X
0 0 0 0 X
1 0 0 0 236
0  0 0 0 236
1  0 0 0 236
0 65242 1 0 X
1 65242 1 0 X
0 0 0 0 X
1 0 0 0 236
0  0 0 0 236
1  0 0 0 236
0 65299 1 0 X
1 65299 1 0 X
0 0 0 0 X
1 0 0 0 236
0  0 0 0 236
1  0 0 0 236
0 65242 1 0 X
1 65242 1 0 X
0 0 0 0 X
1 0 0 0 236
0  0 0 0 236
1  0 0 0 236
0 65411 1 0 X
1 65411 1 0 X
0 0 0 0 X
1 0 0 0 236
0  0 0 0 236
1  0 0 0 236
0 65453 1 0 X
1 65453 1 0 X
0 0 0 0 X
1 0 0 0 236
0  0 0 0 236
1  0 0 0 236
0 65411 1 0 X
1 65411 1 0 X
0 0 0 0 X
1 0 0 0 236
0  0 0 0 236
1  0 0 0 236
0 152 1 0 X
1 152 1 0 X
0 0 0 0 X
1 0 0 0 319
0  0 0 0 319
1  0 0 0 319
0 175 1 0 X
1 175 1 0 X
0 0 0 0 X
1 0 0 0 319
0  0 0 0 319
1  0 0 0 319
0 152 1 0 X
1 152 1 0 X
0 0 0 0 X
1 0 0 0 319
0  0 0 0 319
1  0 0 0 319
0 546 1 0 X
1 546 1 0 X
0 0 0 0 X
1 0 0 0 417
0  0 0 0 417
1  0 0 0 417
0 612 1 0 X
1 612 1 0 X
0 0 0 0 X
1 0 0 0 460
0  0 0 0 460
1  0 0 0 460
0 546 1 0 X
1 546 1 0 X
0 0 0 0 X
1 0 0 0 460
0  0 0 0 460
1  0 0 0 460
0 947 1 0 X
1 947 1 0 X
0 0 0 0 X
1 0 0 0 467
0  0 0 0 467
1  0 0 0 467
0 1033 1 0 X
1 1033 1 0 X
0 0 0 0 X
1 0 0 0 487
0  0 0 0 487
1  0 0 0 487
0 947 1 0 X
1 947 1 0 X
0 0 0 0 X
1 0 0 0 487
0  0 0 0 487
1  0 0 0 487
0 1335 1 0 X
1 1335 1 0 X
0 0 0 0 X
1 0 0 0 487
0  0 0 0 487
1  0 0 0 487
0 1351 1 0 X
1 1351 1 0 X
0 0 0 0 X
1 0 0 0 487
0  0 0 0 487
1  0 0 0 487
0 1335 1 0 X
1 1335 1 0 X
0 0 0 0 X
1 0 0 0 487
0  0 0 0 487
1  0 0 0 487
0 1847 1 0 X
1 1847 1 0 X
0 0 0 0 X
1 0 0 0 528
0  0 0 0 528
1  0 0 0 528
0 1884 1 0 X
1 1884 1 0 X
0 0 0 0 X
1 0 0 0 549
0  0 0 0 549
1  0 0 0 549
0 1847 1 0 X
1 1847 1 0 X
0 0 0 0 X
1 0 0 0 549
0  0 0 0 549
1  0 0 0 549
0 2409 1 0 X
1 2409 1 0 X
0 0 0 0 X
1 0 0 0 599
0  0 0 0 599
1  0 0 0 599
0 2440 1 0 X
1 2440 1 0 X
0 0 0 0 X
1 0 0 0 599
0  0 0 0 599
1  0 0 0 599
0 2409 1 0 X
1 2409 1 0 X
0 0 0 0 X
1 0 0 0 599
0  0 0 0 599
1  0 0 0 599
0 3004 1 0 X
1 3004 1 0 X
0 0 0 0 X
1 0 0 0 626
0  0 0 0 626
1  0 0 0 626
0 3099 1 0 X
1 3099 1 0 X
0 0 0 0 X
1 0 0 0 690
0  0 0 0 690
1  0 0 0 690
0 3004 1 0 X
1 3004 1 0 X
0 0 0 0 X
1 0 0 0 690
0  0 0 0 690
1  0 0 0 690
0 3576 1 0 X
1 3576 1 0 X
0 0 0 0 X
1 0 0 0 690
0  0 0 0 690
1  0 0 0 690
0 3581 1 0 X
1 3581 1 0 X
0 0 0 0 X
1 0 0 0 690
0  0 0 0 690
1  0 0 0 690
0 3576 1 0 X
1 3576 1 0 X
0 0 0 0 X
1 0 0 0 690
0  0 0 0 690
1  0 0 0 690
0 4285 1 0 X
1 4285 1 0 X
0 0 0 0 X
1 0 0 0 714
0  0 0 0 714
1  0 0 0 714
0 4345 1 0 X
1 4345 1 0 X
0 0 0 0 X
1 0 0 0 769
0  0 0 0 769
1  0 0 0 769
0 4285 1 0 X
1 4285 1 0 X
0 0 0 0 X
1 0 0 0 769
0  0 0 0 769
1  0 0 0 769
0 4982 1 0 X
1 4982 1 0 X
0 0 0 0 X
1 0 0 0 769
0  0 0 0 769
1  0 0 0 769
0 5014 1 0 X
1 5014 1 0 X
0 0 0 0 X
1 0 0 0 769
0  0 0 0 769
1  0 0 0 769
0 4982 1 0 X
1 4982 1 0 X
0 0 0 0 X
1 0 0 0 769
0  0 0 0 769
1  0 0 0 769
0 5798 1 0 X
1 5798 1 0 X
0 0 0 0 X
1 0 0 0 848
0  0 0 0 848
1  0 0 0 848
0 5852 1 0 X
1 5852 1 0 X
0 0 0 0 X
1 0 0 0 870
0  0 0 0 870
1  0 0 0 870
0 5798 1 0 X
1 5798 1 0 X
0 0 0 0 X
1 0 0 0 870
0  0 0 0 870
1  0 0 0 870
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*/
