// Digital circuit template_01.dig as structural Verilog
module template_01 (
  input  reset,
  input  clk,
  output A,
  output B,
  output C
);

  wire d_ff_1_q;
  wire [2:0] d_ff_2_q, multiplexer_1_out;

  D_FF d_ff_1 (.D(reset), .C(clk), .Q(d_ff_1_q));  // open: nQ
  Multiplexer #(.Bits(3), .Selector_Bits(3)) multiplexer_1 (
    .sel({C, B, A}), .in_0(3'b011), .in_1(3'b100), .in_2(3'b001), .in_3(3'b110), .in_4(3'b111),
    .in_5(3'b010), .in_6(3'b101), .in_7(3'b000), .out(multiplexer_1_out));
  D_FF #(.Bits(3)) d_ff_2 (.D(multiplexer_1_out), .C(clk), .Q(d_ff_2_q));  // open: nQ
  Multiplexer #(.Bits(3)) multiplexer_2 (.sel(d_ff_1_q), .in_0(d_ff_2_q), .in_1(3'b000), .out({C, B, A}));
endmodule

/* Test case T1:
clk reset C B A
0 0 0 0 0 
0 1 0 0 0
1 1 0 0 0
0 0 0 0 0
1 0 0 1 1
0 0 0 1 1
1 0 1 1 0
0 0 1 1 0 
1 0 1 0 1
0 0 1 0 1
1 0 0 1 0
0 0 0 1 0
1 0 0 0 1
0 0 0 0 1
1 0 1 0 0
0 0 1 0 0
1 0 1 1 1
0 0 1 1 1
1 0 0 0 0
0 0 0 0 0
1 0 0 1 1
0 0 0 1 1
1 0 1 1 0
0 0 1 1 0 
1 0 1 0 1
0 0 1 0 1
1 0 0 1 0
0 0 0 1 0
1 0 0 0 1
0 0 0 0 1
1 0 1 0 0
0 0 1 0 0
1 0 1 1 1
0 0 1 1 1
*/
