// Digital circuit template_02.dig as structural Verilog
module template_02 (
  input  [15:0] A,
  input  \input ,
  input  clk,
  input  [3:0] R,
  output [15:0] nroot,
  output busy
);

  wire and_1_out, and_2_out, and_3_out, and_4_out, and_5_out, and_6_out, and_7_out, and_8_out, and_9_out,
       and_10_out, clk_t, comparator_1_eq, comparator_2_eq, comparator_3_eq, comparator_4_eq,
       comparator_5_eq, comparator_6_lt, comparator_7_eq, comparator_8_eq, comparator_9_eq, comparator_10_eq,
       comparator_11_gt, comparator_12_gt, comparator_13_lt, comparator_14_eq, comparator_15_eq,
       comparator_16_eq, comparator_17_eq, comparator_17_gt, comparator_18_eq, comparator_19_gt, isOverflow,
       multiplexer_1_out, or_1_out, or_2_out, or_3_out, or_4_out, or_5_out;
  wire [2:0] multiplexer_7_out, multiplexer_8_out, multiplexer_9_out, multiplexer_10_out, state;
  wire [3:0] not_1_out, R_t;
  wire [15:0] add_2_s, bef, calc, div_1_q, div_1_r, div_2_q, div_2_r, l, mid, multiplexer_2_out,
       multiplexer_3_out, multiplexer_4_out, multiplexer_5_out, multiplexer_6_out, r_t_t, target;
  wire [31:0] add_3_s, add_4_s, add_5_s, mul_1_mul, mul_2_mul, mul_3_mul, mul_4_mul, multiplexer_11_out,
       multiplexer_12_out, multiplexer_13_out, multiplexer_14_out;

  Comparator #(.Bits(3)) comparator_1 (.a(state), .b(3'b001), .eq(comparator_1_eq));  // open: gt, lt
  Comparator #(.Bits(3)) comparator_2 (.a(state), .b(3'b111), .eq(comparator_2_eq));  // open: gt, lt
  Comparator #(.Bits(3)) comparator_3 (.a(state), .b(3'b001), .eq(comparator_3_eq));  // open: gt, lt
  Comparator #(.Bits(3)) comparator_4 (.a(state), .b(3'b001), .eq(comparator_4_eq));  // open: gt, lt
  Comparator #(.Bits(3)) comparator_5 (.a(state), .b(3'b001), .eq(comparator_5_eq));  // open: gt, lt
  Comparator #(.Bits(3)) comparator_6 (.a(state), .b(3'b010), .lt(comparator_6_lt));  // open: gt, eq
  or or_1 (or_1_out, comparator_1_eq, comparator_2_eq);
  and and_1 (and_1_out, comparator_3_eq, clk_t);
  and and_2 (and_2_out, comparator_4_eq, clk_t);
  D_FF #(.Bits(16)) d_ff_1 (.D(A), .C(and_1_out), .Q(target));  // open: nQ
  D_FF #(.Bits(4)) d_ff_2 (.D(R), .C(and_2_out), .Q(R_t));  // open: nQ
  Multiplexer multiplexer_1 (.sel(comparator_5_eq), .in_0(1'b0), .in_1(1'b1), .out(multiplexer_1_out));
  and and_3 (and_3_out, comparator_6_lt, clk_t);
  Multiplexer #(.Bits(16)) multiplexer_2 (
    .sel(comparator_2_eq), .in_0({16{1'b0}}), .in_1(mid), .out(multiplexer_2_out));
  and and_4 (and_4_out, or_1_out, clk_t);
  // Probe on target
  // Probe on R_t
  D_FF d_ff_3 (.D(multiplexer_1_out), .C(and_3_out), .Q(busy));  // open: nQ
  D_FF #(.Bits(16)) d_ff_4 (.D(multiplexer_2_out), .C(and_4_out), .Q(bef));  // open: nQ
  // Probe on bef
  // Probe on mid
  // Probe on calc
  // Probe on state
  Div #(.Bits(16)) div_1 (.a(l), .b(16'h2), .q(div_1_q), .r(div_1_r));
  Div #(.Bits(16)) div_2 (.a(r_t_t), .b(16'h2), .q(div_2_q), .r(div_2_r));
  Comparator #(.Bits(3)) comparator_7 (.a(state), .b(3'b001), .eq(comparator_7_eq));  // open: gt, lt
  Comparator #(.Bits(3)) comparator_8 (.a(state), .b(3'b110), .eq(comparator_8_eq));  // open: gt, lt
  Comparator #(.Bits(3)) comparator_9 (.a(state), .b(3'b001), .eq(comparator_9_eq));  // open: gt, lt
  Comparator #(.Bits(3)) comparator_10 (.a(state), .b(3'b101), .eq(comparator_10_eq));  // open: gt, lt
  Comparator #(.Bits(16)) comparator_11 (.a(div_1_r), .b({16{1'b0}}), .gt(comparator_11_gt));  // open: eq, lt
  Comparator #(.Bits(16)) comparator_12 (.a(div_2_r), .b({16{1'b0}}), .gt(comparator_12_gt));  // open: eq, lt
  Comparator #(.Bits(16)) comparator_13 (.a(calc), .b(target), .lt(comparator_13_lt));  // open: gt, eq
  Multiplexer #(.Bits(16)) multiplexer_3 (.sel(comparator_8_eq), .in_0(l), .in_1(mid), .out(multiplexer_3_out));
  or or_2 (or_2_out, comparator_7_eq, comparator_8_eq);
  Multiplexer #(.Bits(16)) multiplexer_4 (.sel(comparator_10_eq), .in_0(r_t_t), .in_1(mid), .out(multiplexer_4_out));
  or or_3 (or_3_out, comparator_9_eq, comparator_10_eq);
  and and_5 (and_5_out, comparator_11_gt, comparator_12_gt);
  // Probe on R_t
  // Probe on isOverflow
  Add #(.Bits(16)) add_1 (.a({16{1'b0}}), .b({16{1'b0}}), .c_i(comparator_13_lt));  // open: s, c_o
  Comparator #(.Bits(3)) comparator_14 (.a(state), .b(3'b010), .eq(comparator_14_eq));  // open: gt, lt
  Multiplexer #(.Bits(16)) multiplexer_5 (
    .sel(comparator_7_eq), .in_0(multiplexer_3_out), .in_1({16{1'b0}}), .out(multiplexer_5_out));
  and and_6 (and_6_out, or_2_out, clk_t);
  Multiplexer #(.Bits(16)) multiplexer_6 (
    .sel(comparator_9_eq), .in_0(multiplexer_4_out), .in_1({16{1'b1}}), .out(multiplexer_6_out));
  and and_7 (and_7_out, or_3_out, clk_t);
  Add #(.Bits(16)) add_2 (.a(div_1_q), .b(div_2_q), .c_i(and_5_out), .s(add_2_s));  // open: c_o
  and and_8 (and_8_out, comparator_14_eq, clk_t);
  D_FF #(.Bits(16)) d_ff_5 (.D(multiplexer_5_out), .C(and_6_out), .Q(l));  // open: nQ
  D_FF #(.Bits(16)) d_ff_6 (.D(multiplexer_6_out), .C(and_7_out), .Q(r_t_t));  // open: nQ
  D_FF #(.Bits(16)) d_ff_7 (.D(add_2_s), .C(and_8_out), .Q(mid));  // open: nQ
  // Probe on l
  // Probe on r_t_t
  // Probe on mid
  Multiplexer #(.Bits(3)) multiplexer_7 (.sel(\input ), .in_0(3'b000), .in_1(3'b001), .out(multiplexer_7_out));
  Comparator #(.Bits(3)) comparator_15 (.a(state), .b(3'b000), .eq(comparator_15_eq));  // open: gt, lt
  Comparator #(.Bits(16)) comparator_16 (.a(l), .b(r_t_t), .eq(comparator_16_eq));  // open: gt, lt
  Comparator #(.Bits(16)) comparator_17 (
    .a(calc), .b(target), .gt(comparator_17_gt), .eq(comparator_17_eq));  // open: lt
  and and_9 (and_9_out, comparator_15_eq, clk_t);
  or or_4 (or_4_out, comparator_16_eq, comparator_17_eq);
  Mul #(.Bits(16)) mul_1 (.a(mid), .b(16'h1), .mul(mul_1_mul));
  Mul #(.Bits(16)) mul_2 (.a(mul_1_mul[15:0]), .b(mid), .mul(mul_2_mul));
  Mul #(.Bits(16)) mul_3 (.a(mul_2_mul[15:0]), .b(mid), .mul(mul_3_mul));
  Mul #(.Bits(16)) mul_4 (.a(mul_3_mul[15:0]), .b(mid), .mul(mul_4_mul));
  D_FF #(.Bits(16)) d_ff_8 (.D(calc), .C(and_9_out), .Q(nroot));  // open: nQ
  or or_5 (or_5_out, comparator_17_gt, isOverflow);
  // Probe on mul_1_mul
  // Probe on mul_2_mul
  // Probe on mul_3_mul
  // Probe on mul_4_mul
  Multiplexer #(.Bits(3)) multiplexer_8 (.sel(or_4_out), .in_0(3'b100), .in_1(3'b000), .out(multiplexer_8_out));
  Multiplexer #(.Bits(3)) multiplexer_9 (.sel(or_5_out), .in_0(3'b110), .in_1(3'b101), .out(multiplexer_9_out));
  assign not_1_out = ~R_t;  // Not not_1, 4 bits wide
  Multiplexer #(.Selector_Bits(3), .Bits(3)) multiplexer_10 (
    .sel(state), .in_0(multiplexer_7_out), .in_1(3'b010), .in_2(3'b011), .in_3(multiplexer_8_out),
    .in_4(multiplexer_9_out), .in_5(3'b111), .in_6(3'b111), .in_7(3'b010), .out(multiplexer_10_out));
  Multiplexer #(.Bits(32)) multiplexer_11 (
    .sel(not_1_out[0]), .in_0(mul_1_mul), .in_1({32{1'b0}}), .out(multiplexer_11_out));
  Multiplexer #(.Bits(32)) multiplexer_12 (
    .sel(not_1_out[1]), .in_0(mul_2_mul), .in_1({32{1'b0}}), .out(multiplexer_12_out));
  Multiplexer #(.Bits(32)) multiplexer_13 (
    .sel(not_1_out[2]), .in_0(mul_3_mul), .in_1({32{1'b0}}), .out(multiplexer_13_out));
  Multiplexer #(.Bits(32)) multiplexer_14 (
    .sel(not_1_out[3]), .in_0(mul_4_mul), .in_1({32{1'b0}}), .out(multiplexer_14_out));
  Add #(.Bits(32)) add_3 (.a(multiplexer_11_out), .b(multiplexer_12_out), .c_i(1'b0), .s(add_3_s));  // open: c_o
  Add #(.Bits(32)) add_4 (.a(multiplexer_13_out), .b(multiplexer_14_out), .c_i(1'b0), .s(add_4_s));  // open: c_o
  D_FF #(.Bits(3)) d_ff_9 (.D(multiplexer_10_out), .C(clk), .Q(state));  // open: nQ
  not not_2 (clk_t, clk);
  Add #(.Bits(32)) add_5 (.a(add_3_s), .b(add_4_s), .c_i(1'b0), .s(add_5_s));  // open: c_o
  // Probe on state
  // Probe on add_5_s
  Comparator #(.Bits(3)) comparator_18 (.a(state), .b(3'b011), .eq(comparator_18_eq));  // open: gt, lt
  // Probe on add_5_s[15:0]
  // Probe on add_5_s[31:16]
  Comparator #(.Bits(16)) comparator_19 (.a(add_5_s[31:16]), .b({16{1'b0}}), .gt(comparator_19_gt));  // open: eq, lt
  and and_10 (and_10_out, comparator_18_eq, clk_t);
  D_FF #(.Bits(16)) d_ff_10 (.D(add_5_s[15:0]), .C(and_10_out), .Q(calc));  // open: nQ
  D_FF d_ff_11 (.D(comparator_19_gt), .C(and_10_out), .Q(isOverflow));  // open: nQ
  // Probe on calc

  // Notes on the sheet:
  //   clk: Hz: 200
endmodule

/* Test case TestCase1:
clk A R input nroot busy
0 0 0 0 X 0
1 0 0 0 X 0
0 0 0 0 X 0
1 0 0 0 X 0
0 2 2 1 X X
1 2 2 1 X X
repeat (255) C 2 2 0 X X
0 2 2 0 1 0
1 2 2 0 1 0
0 0 0 0 X 0
1 0 0 0 X 0
0 0 0 0 X 0
1 0 0 0 X 0
0 4 2 1 X X
1 4 2 1 X X
repeat (255) C 4 2 0 X X
0 4 2 0 2 0
1 4 2 0 2 0
0 0 0 0 X 0
1 0 0 0 X 0
0 0 0 0 X 0
1 0 0 0 X 0
0 8 2 1 X X
1 8 2 1 X X
repeat (255) C 8 2 0 X X
0 8 2 0 2 0
1 8 2 0 2 0
0 0 0 0 X 0
1 0 0 0 X 0
0 0 0 0 X 0
1 0 0 0 X 0
0 16 2 1 X X
1 16 2 1 X X
repeat (255) C 16 2 0 X X
0 16 2 0 4 0
1 16 2 0 4 0
*/

/* Test case TestCase4:
clk A R input nroot busy
0 0 0 0 X 0
1 0 0 0 X 0
0 0 0 0 X 0
1 0 0 0 X 0
0 65530 12 1 X X
1 65530 12 1 X X
repeat (255) C 65530 12 0 X X
0 65530 12 0 2 0
1 65530 12 0 2 0
0 0 0 0 X 0
1 0 0 0 X 0
0 0 0 0 X 0
1 0 0 0 X 0
0 60000 3 1 X X
1 60000 3 1 X X
repeat (255) C 60000 3 0 X X
0 60000 3 0 39 0
1 60000 3 0 39 0
0 0 0 0 X 0
1 0 0 0 X 0
0 0 0 0 X 0
1 0 0 0 X 0
0 55124 4 1 X X
1 55124 4 1 X X
repeat (255) C 55124 4 0 X X
0 55124 4 0 15 0
1 55124 4 0 15 0
0 0 0 0 X 0
1 0 0 0 X 0
0 0 0 0 X 0
1 0 0 0 X 0
0 14778 5 1 X X
1 14778 5 1 X X
repeat (255) C 14778 5 0 X X
0 14778 5 0 6 0
1 14778 5 0 6 0
*/

/* Test case TestCase8:
clk A R input nroot busy
0 0 0 0 X 0
1 0 0 0 X 0
0 0 0 0 X 0
1 0 0 0 X 0
0 65535 1 1 X X
1 65535 1 1 X X
repeat (255) C 65535 1 0 X X
0 65535 1 0 65535 0
1 65535 1 0 65535 0
0 0 0 0 X 0
1 0 0 0 X 0
0 0 0 0 X 0
1 0 0 0 X 0
0 64000 15 1 X X
1 64000 15 1 X X
repeat (255) C 64000 15 0 X X
0 64000 15 0 2 0
1 64000 15 0 2 0
0 0 0 0 X 0
1 0 0 0 X 0
0 0 0 0 X 0
1 0 0 0 X 0
0 12000 5 1 X X
1 12000 5 1 X X
repeat (255) C 12000 5 0 X X
0 12000 5 0 6 0
1 12000 5 0 6 0
0 0 0 0 X 0
1 0 0 0 X 0
0 0 0 0 X 0
1 0 0 0 X 0
0 65535 15 1 X X
1 65535 15 1 X X
repeat (255) C 65535 15 0 X X
0 65535 15 0 2 0
1 65535 15 0 2 0
*/
