// Digital circuit template_03.dig as structural Verilog
module template_03 (
  input  [15:0] A,
  input  \input ,
  input  clk,
  input  reset,
  output [17:0] peak
);

  wire and_2_out, clkInp, comparator_1_lt, comparator_2_eq, comparator_2_lt, comparator_3_gt,
       comparator_4_gt, or_1_out;
  wire [1:0] multiplexer_7_out, multiplexer_8_out, multiplexer_9_out, multiplexer_10_out, multiplexer_11_out,
       state2, stateCycle;
  wire [14:0] add_1_s, not_1_out;
  wire [16:0] add_2_s, not_2_out;
  wire [17:0] add_3_s, add_4_s, d_ff_1_q, d_ff_2_q, multiplexer_1_out, multiplexer_2_out, multiplexer_3_out,
       multiplexer_4_out, multiplexer_5_out, multiplexer_6_out, multiplexer_12_out, not_3_out, Now_1_q,
       Now_q, sub_1_s, sub_2_s;

  assign not_1_out = ~A[14:0];  // Not not_1, 15 bits wide
  Add #(.Bits(15)) add_1 (.a(not_1_out), .b(15'h1), .c_i(1'b0), .s(add_1_s));  // open: c_o
  assign not_2_out = ~{2'b00, add_1_s};  // Not not_2, 17 bits wide
  Add #(.Bits(17)) add_2 (.a(not_2_out), .b(17'h1), .c_i(1'b0), .s(add_2_s));  // open: c_o
  Multiplexer #(.Bits(18)) multiplexer_1 (
    .sel(A[15]), .in_0({2'b00, A}), .in_1({1'b1, add_2_s}), .out(multiplexer_1_out));
  // Probe on multiplexer_1_out
  D_FF #(.Bits(18)) Now (.D(multiplexer_1_out), .C(clkInp), .Q(Now_q));  // open: nQ
  Sub #(.Bits(18)) sub_1 (.a(multiplexer_4_out), .b(multiplexer_2_out), .c_i(1'b0), .s(sub_1_s));  // open: c_o
  and and_1 (clkInp, \input , clk);
  Multiplexer #(.Bits(18)) multiplexer_2 (.sel(reset), .in_0(Now_q), .in_1({18{1'b0}}), .out(multiplexer_2_out));
  assign not_3_out = ~sub_1_s;  // Not not_3, 18 bits wide
  Add #(.Bits(18)) add_3 (.a(not_3_out), .b(18'h1), .c_i(1'b0), .s(add_3_s));  // open: c_o
  // Probe on multiplexer_2_out
  Comparator #(.Signed("true"), .Bits(18)) comparator_1 (
    .a(sub_1_s), .b({18{1'b0}}), .lt(comparator_1_lt));  // open: gt, eq
  D_FF #(.Bits(18)) Now_1 (.D(multiplexer_2_out), .C(clkInp), .Q(Now_1_q));  // open: nQ
  Multiplexer #(.Bits(18)) multiplexer_3 (
    .sel(comparator_1_lt), .in_0(sub_1_s), .in_1(add_3_s), .out(multiplexer_3_out));
  Multiplexer #(.Bits(18)) multiplexer_4 (.sel(reset), .in_0(Now_1_q), .in_1({18{1'b0}}), .out(multiplexer_4_out));
  // Probe on multiplexer_3_out
  D_FF #(.Bits(18)) d_ff_1 (.D(multiplexer_3_out), .C(~clkInp), .Q(d_ff_1_q));  // open: nQ
  // Probe on multiplexer_4_out
  Multiplexer #(.Bits(18)) multiplexer_5 (.sel(reset), .in_0(d_ff_1_q), .in_1({18{1'b0}}), .out(multiplexer_5_out));
  // Probe on multiplexer_5_out
  D_FF #(.Bits(18)) d_ff_2 (.D(multiplexer_5_out), .C(~clkInp), .Q(d_ff_2_q));  // open: nQ
  Multiplexer #(.Bits(18)) multiplexer_6 (.sel(reset), .in_0(d_ff_2_q), .in_1({18{1'b0}}), .out(multiplexer_6_out));
  Multiplexer #(.Selector_Bits(2), .Bits(2)) multiplexer_7 (
    .sel(state2), .in_0(2'b01), .in_1(2'b10), .in_2(2'b11), .in_3(2'b11), .out(multiplexer_7_out));
  // Probe on multiplexer_6_out
  Multiplexer #(.Selector_Bits(2), .Bits(2)) multiplexer_8 (
    .sel(stateCycle), .in_0(2'b01), .in_1(2'b10), .in_2(2'b11), .in_3(2'b00), .out(multiplexer_8_out));
  Multiplexer #(.Bits(2)) multiplexer_9 (.sel(reset), .in_0(multiplexer_7_out), .in_1(2'b00), .out(multiplexer_9_out));
  Add #(.Bits(18)) add_4 (.a(multiplexer_5_out), .b(multiplexer_6_out), .c_i(1'b0), .s(add_4_s));  // open: c_o
  Sub #(.Bits(18)) sub_2 (.a(18'ha), .b(18'h3fff7), .c_i(1'b0), .s(sub_2_s));  // open: c_o
  Multiplexer #(.Bits(2)) multiplexer_10 (
    .sel(\input ), .in_0(multiplexer_8_out), .in_1(2'b00), .out(multiplexer_10_out));
  // Probe on add_4_s
  D_FF #(.Bits(2)) d_ff_3 (.D(multiplexer_9_out), .C(clkInp), .Q(state2));  // open: nQ
  Comparator #(.Signed("true"), .Bits(18)) comparator_2 (
    .a(add_4_s), .b(peak), .eq(comparator_2_eq), .lt(comparator_2_lt));  // open: gt
  // Probe on sub_2_s
  Multiplexer #(.Bits(2)) multiplexer_11 (
    .sel(reset), .in_0(multiplexer_10_out), .in_1(2'b00), .out(multiplexer_11_out));
  or or_1 (or_1_out, comparator_2_eq, comparator_2_lt);
  D_FF #(.Bits(2)) d_ff_4 (.D(multiplexer_11_out), .C(clk), .Q(stateCycle));  // open: nQ
  Multiplexer #(.Bits(18)) multiplexer_12 (.sel(or_1_out), .in_0(add_4_s), .in_1(peak), .out(multiplexer_12_out));
  Comparator #(.Bits(2)) comparator_3 (.a(state2), .b(2'b10), .gt(comparator_3_gt));  // open: eq, lt
  Comparator #(.Bits(2)) comparator_4 (.a(stateCycle), .b(2'b00), .gt(comparator_4_gt));  // open: eq, lt
  D_FF #(.Bits(18)) d_ff_5 (.D(multiplexer_12_out), .C(and_2_out), .Q(peak));  // open: nQ
  and and_2 (and_2_out, comparator_3_gt, comparator_4_gt);

  // Notes on the sheet:
  //   clk: Hz: 200
endmodule

/* Test case Testcase1:
clk A input reset peak
0 0 0 0 0
1 0 0 0 0
0 0 0 1 0
1 0 0 1 0
0 0  0 0 0
1 0  0 0 0
0 5 1 0 X
1 5 1 0 X
0 0 0 0 X
1 0 0 0 X
0 1 1 0 X
1 1 1 0 X
0 0 0 0 X
1 0 0 0 X
0 0 0 0 X
1 0 0 0 X
0 2 1 0 X
1 2 1 0 X
0 0 0 0 X
1 0 0 0 X
0  0 0 0 5
1  0 0 0 5
0 10 1 0 X
1 10 1 0 X
0 0 0 0 X
1 0 0 0 9
0  0 0 0 9
1  0 0 0 9
0 3 1 0 X
1 3 1 0 X
0 0 0 0 X
1 0 0 0 15
0  0 0 0 15
1  0 0 0 15
0 65526 1 0 X
1 65526 1 0 X
0 0 0 0 X
1 0 0 0 20
0  0 0 0 20
1  0 0 0 20
0 2 1 0 X
1 2 1 0 X
0 0 0 0 X
1 0 0 0 25
0  0 0 0 25
1  0 0 0 25
0 4 1 0 X
1 4 1 0 X
0 0 0 0 X
1 0 0 0 25
0  0 0 0 25
1  0 0 0 25
0 1 1 0 X
1 1 1 0 X
0 0 0 0 X
1 0 0 0 25
0  0 0 0 25
1  0 0 0 25
0 2 1 0 X
1 2 1 0 X
0 0 0 0 X
1 0 0 0 25
*/

/* Test case Testcase3:
clk A input reset peak
0 0 0 0 0
1 0 0 0 0
0 0 0 1 0
1 0 0 1 0
0 0  0 0 0
1 0  0 0 0
0 9924 1 0 X
1 9924 1 0 X
0 0 0 0 X
1 0 0 0 X
0 1714 1 0 X
1 1714 1 0 X
0 0 0 0 X
1 0 0 0 X
0 0 0 0 X
1 0 0 0 X
0 19734 1 0 X
1 19734 1 0 X
0 0 0 0 X
1 0 0 0 X
0  0 0 0 26230
1  0 0 0 26230
0 14144 1 0 X
1 14144 1 0 X
0 0 0 0 X
1 0 0 0 26230
0  0 0 0 26230
1  0 0 0 26230
0 6348 1 0 X
1 6348 1 0 X
0 0 0 0 X
1 0 0 0 26230
0  0 0 0 26230
1  0 0 0 26230
0 29200 1 0 X
1 29200 1 0 X
0 0 0 0 X
1 0 0 0 30648
0  0 0 0 30648
1  0 0 0 30648
0 13658 1 0 X
1 13658 1 0 X
0 0 0 0 X
1 0 0 0 38394
0  0 0 0 38394
1  0 0 0 38394
0 20001 1 0 X
1 20001 1 0 X
0 0 0 0 X
1 0 0 0 38394
0  0 0 0 38394
1  0 0 0 38394
0 23323 1 0 X
1 23323 1 0 X
0 0 0 0 X
1 0 0 0 38394
0  0 0 0 38394
1  0 0 0 38394
0 15516 1 0 X
1 15516 1 0 X
0 0 0 0 X
1 0 0 0 38394
0  0 0 0 38394
1  0 0 0 38394
0 26104 1 0 X
1 26104 1 0 X
0 0 0 0 X
1 0 0 0 38394
0  0 0 0 38394
1  0 0 0 38394
0 23576 1 0 X
1 23576 1 0 X
0 0 0 0 X
1 0 0 0 38394
0  0 0 0 38394
1  0 0 0 38394
0 15152 1 0 X
1 15152 1 0 X
0 0 0 0 X
1 0 0 0 38394
0  0 0 0 38394
1  0 0 0 38394
0 9762 1 0 X
1 9762 1 0 X
0 0 0 0 X
1 0 0 0 38394
0  0 0 0 38394
1  0 0 0 38394
0 3599 1 0 X
1 3599 1 0 X
0 0 0 0 X
1 0 0 0 38394
0  0 0 0 38394
1  0 0 0 38394
0 16576 1 0 X
1 16576 1 0 X
0 0 0 0 X
1 0 0 0 38394
0  0 0 0 38394
1  0 0 0 38394
0 30162 1 0 X
1 30162 1 0 X
0 0 0 0 X
1 0 0 0 38394
0  0 0 0 38394
1  0 0 0 38394
0 30934 1 0 X
1 30934 1 0 X
0 0 0 0 X
1 0 0 0 38394
0  0 0 0 38394
1  0 0 0 38394
0 31029 1 0 X
1 31029 1 0 X
0 0 0 0 X
1 0 0 0 38394
0  0 0 0 38394
1  0 0 0 38394
0 18783 1 0 X
1 18783 1 0 X
0 0 0 0 X
1 0 0 0 38394
0  0 0 0 38394
1  0 0 0 38394
0 1881 1 0 X
1 1881 1 0 X
0 0 0 0 X
1 0 0 0 38394
0  0 0 0 38394
1  0 0 0 38394
0 10695 1 0 X
1 10695 1 0 X
0 0 0 0 X
1 0 0 0 38394
0  0 0 0 38394
1  0 0 0 38394
0 7756 1 0 X
1 7756 1 0 X
0 0 0 0 X
1 0 0 0 38394
0  0 0 0 38394
1  0 0 0 38394
0 14129 1 0 X
1 14129 1 0 X
0 0 0 0 X
1 0 0 0 38394
0  0 0 0 38394
1  0 0 0 38394
0 30596 1 0 X
1 30596 1 0 X
0 0 0 0 X
1 0 0 0 38394
0  0 0 0 38394
1  0 0 0 38394
0 21070 1 0 X
1 21070 1 0 X
0 0 0 0 X
1 0 0 0 38394
0  0 0 0 38394
1  0 0 0 38394
0 15427 1 0 X
1 15427 1 0 X
0 0 0 0 X
1 0 0 0 38394
0  0 0 0 38394
1  0 0 0 38394
0 2565 1 0 X
1 2565 1 0 X
0 0 0 0 X
1 0 0 0 38394
0  0 0 0 38394
1  0 0 0 38394
0 24554 1 0 X
1 24554 1 0 X
0 0 0 0 X
1 0 0 0 38394
0  0 0 0 38394
1  0 0 0 38394
0 25370 1 0 X
1 25370 1 0 X
0 0 0 0 X
1 0 0 0 38394
0  0 0 0 38394
1  0 0 0 38394
0 9273 1 0 X
1 9273 1 0 X
0 0 0 0 X
1 0 0 0 38394
0  0 0 0 38394
1  0 0 0 38394
0 8302 1 0 X
1 8302 1 0 X
0 0 0 0 X
1 0 0 0 38394
0  0 0 0 38394
1  0 0 0 38394
0 3282 1 0 X
1 3282 1 0 X
0 0 0 0 X
1 0 0 0 38394
0  0 0 0 38394
1  0 0 0 38394
0 25633 1 0 X
1 25633 1 0 X
0 0 0 0 X
1 0 0 0 38394
0  0 0 0 38394
1  0 0 0 38394
0 13448 1 0 X
1 13448 1 0 X
0 0 0 0 X
1 0 0 0 38394
0  0 0 0 38394
1  0 0 0 38394
0 5516 1 0 X
1 5516 1 0 X
0 0 0 0 X
1 0 0 0 38394
0  0 0 0 38394
1  0 0 0 38394
0 31976 1 0 X
1 31976 1 0 X
0 0 0 0 X
1 0 0 0 38394
0  0 0 0 38394
1  0 0 0 38394
0 24271 1 0 X
1 24271 1 0 X
0 0 0 0 X
1 0 0 0 38394
0  0 0 0 38394
1  0 0 0 38394
0 6215 1 0 X
1 6215 1 0 X
0 0 0 0 X
1 0 0 0 38394
0  0 0 0 38394
1  0 0 0 38394
0 10282 1 0 X
1 10282 1 0 X
0 0 0 0 X
1 0 0 0 38394
0  0 0 0 38394
1  0 0 0 38394
0 28448 1 0 X
1 28448 1 0 X
0 0 0 0 X
1 0 0 0 38394
0  0 0 0 38394
1  0 0 0 38394
0 19282 1 0 X
1 19282 1 0 X
0 0 0 0 X
1 0 0 0 38394
0  0 0 0 38394
1  0 0 0 38394
0 16410 1 0 X
1 16410 1 0 X
0 0 0 0 X
1 0 0 0 38394
0  0 0 0 38394
1  0 0 0 38394
0 4699 1 0 X
1 4699 1 0 X
0 0 0 0 X
1 0 0 0 38394
0  0 0 0 38394
1  0 0 0 38394
0 17855 1 0 X
1 17855 1 0 X
0 0 0 0 X
1 0 0 0 38394
0  0 0 0 38394
1  0 0 0 38394
0 7295 1 0 X
1 7295 1 0 X
0 0 0 0 X
1 0 0 0 38394
0  0 0 0 38394
1  0 0 0 38394
0 5567 1 0 X
1 5567 1 0 X
0 0 0 0 X
1 0 0 0 38394
0  0 0 0 38394
1  0 0 0 38394
0 5318 1 0 X
1 5318 1 0 X
0 0 0 0 X
1 0 0 0 38394
0  0 0 0 38394
1  0 0 0 38394
0 7523 1 0 X
1 7523 1 0 X
0 0 0 0 X
1 0 0 0 38394
0  0 0 0 38394
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*/

/* Test case Testcase6:
clk A input reset peak
0 0 0 0 0
1 0 0 0 0
0 0 0 1 0
1 0 0 1 0
0 0  0 0 0
1 0  0 0 0
0 64563 1 0 X
1 64563 1 0 X
0 0 0 0 X
1 0 0 0 X
0 64536 1 0 X
1 64536 1 0 X
0 0 0 0 X
1 0 0 0 X
0 0 0 0 X
1 0 0 0 X
0 64709 1 0 X
1 64709 1 0 X
0 0 0 0 X
1 0 0 0 X
0  0 0 0 200
1  0 0 0 200
0 64724 1 0 X
1 64724 1 0 X
0 0 0 0 X
1 0 0 0 200
0  0 0 0 200
1  0 0 0 200
0 64709 1 0 X
1 64709 1 0 X
0 0 0 0 X
1 0 0 0 200
0  0 0 0 200
1  0 0 0 200
0 64804 1 0 X
1 64804 1 0 X
0 0 0 0 X
1 0 0 0 200
0  0 0 0 200
1  0 0 0 200
0 64890 1 0 X
1 64890 1 0 X
0 0 0 0 X
1 0 0 0 200
0  0 0 0 200
1  0 0 0 200
0 64804 1 0 X
1 64804 1 0 X
0 0 0 0 X
1 0 0 0 200
0  0 0 0 200
1  0 0 0 200
0 64917 1 0 X
1 64917 1 0 X
0 0 0 0 X
1 0 0 0 200
0  0 0 0 200
1  0 0 0 200
0 64968 1 0 X
1 64968 1 0 X
0 0 0 0 X
1 0 0 0 200
0  0 0 0 200
1  0 0 0 200
0 64917 1 0 X
1 64917 1 0 X
0 0 0 0 X
1 0 0 0 200
0  0 0 0 200
1  0 0 0 200
0 65085 1 0 X
1 65085 1 0 X
0 0 0 0 X
1 0 0 0 219
0  0 0 0 219
1  0 0 0 219
0 65153 1 0 X
1 65153 1 0 X
0 0 0 0 X
1 0 0 0 236
0  0 0 0 236
1  0 0 0 236
0 65085 1 0 X
1 65085 1 0 X
0 0 0 0 X
1 0 0 0 236
0  0 0 0 236
1  0 0 0 236
0 65242 1 0 X
1 65242 1 0 X
0 0 0 0 X
1 0 0 0 236
0  0 0 0 236
1  0 0 0 236
0 65299 1 0 X
1 65299 1 0 X
0 0 0 0 X
1 0 0 0 236
0  0 0 0 236
1  0 0 0 236
0 65242 1 0 X
1 65242 1 0 X
0 0 0 0 X
1 0 0 0 236
0  0 0 0 236
1  0 0 0 236
0 65411 1 0 X
1 65411 1 0 X
0 0 0 0 X
1 0 0 0 236
0  0 0 0 236
1  0 0 0 236
0 65453 1 0 X
1 65453 1 0 X
0 0 0 0 X
1 0 0 0 236
0  0 0 0 236
1  0 0 0 236
0 65411 1 0 X
1 65411 1 0 X
0 0 0 0 X
1 0 0 0 236
0  0 0 0 236
1  0 0 0 236
0 152 1 0 X
1 152 1 0 X
0 0 0 0 X
1 0 0 0 319
0  0 0 0 319
1  0 0 0 319
0 175 1 0 X
1 175 1 0 X
0 0 0 0 X
1 0 0 0 319
0  0 0 0 319
1  0 0 0 319
0 152 1 0 X
1 152 1 0 X
0 0 0 0 X
1 0 0 0 319
0  0 0 0 319
1  0 0 0 319
0 546 1 0 X
1 546 1 0 X
0 0 0 0 X
1 0 0 0 417
0  0 0 0 417
1  0 0 0 417
0 612 1 0 X
1 612 1 0 X
0 0 0 0 X
1 0 0 0 460
0  0 0 0 460
1  0 0 0 460
0 546 1 0 X
1 546 1 0 X
0 0 0 0 X
1 0 0 0 460
0  0 0 0 460
1  0 0 0 460
0 947 1 0 X
1 947 1 0 X
0 0 0 0 X
1 0 0 0 467
0  0 0 0 467
1  0 0 0 467
0 1033 1 0 X
1 1033 1 0 X
0 0 0 0 X
1 0 0 0 487
0  0 0 0 487
1  0 0 0 487
0 947 1 0 X
1 947 1 0 X
0 0 0 0 X
1 0 0 0 487
0  0 0 0 487
1  0 0 0 487
0 1335 1 0 X
1 1335 1 0 X
0 0 0 0 X
1 0 0 0 487
0  0 0 0 487
1  0 0 0 487
0 1351 1 0 X
1 1351 1 0 X
0 0 0 0 X
1 0 0 0 487
0  0 0 0 487
1  0 0 0 487
0 1335 1 0 X
1 1335 1 0 X
0 0 0 0 X
1 0 0 0 487
0  0 0 0 487
1  0 0 0 487
0 1847 1 0 X
1 1847 1 0 X
0 0 0 0 X
1 0 0 0 528
0  0 0 0 528
1  0 0 0 528
0 1884 1 0 X
1 1884 1 0 X
0 0 0 0 X
1 0 0 0 549
0  0 0 0 549
1  0 0 0 549
0 1847 1 0 X
1 1847 1 0 X
0 0 0 0 X
1 0 0 0 549
0  0 0 0 549
1  0 0 0 549
0 2409 1 0 X
1 2409 1 0 X
0 0 0 0 X
1 0 0 0 599
0  0 0 0 599
1  0 0 0 599
0 2440 1 0 X
1 2440 1 0 X
0 0 0 0 X
1 0 0 0 599
0  0 0 0 599
1  0 0 0 599
0 2409 1 0 X
1 2409 1 0 X
0 0 0 0 X
1 0 0 0 599
0  0 0 0 599
1  0 0 0 599
0 3004 1 0 X
1 3004 1 0 X
0 0 0 0 X
1 0 0 0 626
0  0 0 0 626
1  0 0 0 626
0 3099 1 0 X
1 3099 1 0 X
0 0 0 0 X
1 0 0 0 690
0  0 0 0 690
1  0 0 0 690
0 3004 1 0 X
1 3004 1 0 X
0 0 0 0 X
1 0 0 0 690
0  0 0 0 690
1  0 0 0 690
0 3576 1 0 X
1 3576 1 0 X
0 0 0 0 X
1 0 0 0 690
0  0 0 0 690
1  0 0 0 690
0 3581 1 0 X
1 3581 1 0 X
0 0 0 0 X
1 0 0 0 690
0  0 0 0 690
1  0 0 0 690
0 3576 1 0 X
1 3576 1 0 X
0 0 0 0 X
1 0 0 0 690
0  0 0 0 690
1  0 0 0 690
0 4285 1 0 X
1 4285 1 0 X
0 0 0 0 X
1 0 0 0 714
0  0 0 0 714
1  0 0 0 714
0 4345 1 0 X
1 4345 1 0 X
0 0 0 0 X
1 0 0 0 769
0  0 0 0 769
1  0 0 0 769
0 4285 1 0 X
1 4285 1 0 X
0 0 0 0 X
1 0 0 0 769
0  0 0 0 769
1  0 0 0 769
0 4982 1 0 X
1 4982 1 0 X
0 0 0 0 X
1 0 0 0 769
0  0 0 0 769
1  0 0 0 769
0 5014 1 0 X
1 5014 1 0 X
0 0 0 0 X
1 0 0 0 769
0  0 0 0 769
1  0 0 0 769
0 4982 1 0 X
1 4982 1 0 X
0 0 0 0 X
1 0 0 0 769
0  0 0 0 769
1  0 0 0 769
0 5798 1 0 X
1 5798 1 0 X
0 0 0 0 X
1 0 0 0 848
0  0 0 0 848
1  0 0 0 848
0 5852 1 0 X
1 5852 1 0 X
0 0 0 0 X
1 0 0 0 870
0  0 0 0 870
1  0 0 0 870
0 5798 1 0 X
1 5798 1 0 X
0 0 0 0 X
1 0 0 0 870
0  0 0 0 870
1  0 0 0 870
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*/
