// Digital circuit 01.dig as structural Verilog
module _01 (
  input  [2:0] A,
  input  [2:0] B
);

  wire add_1_c_o, and_1_out, and_2_out, not_1_out, or_1_out;
  wire [2:0] add_1_s;

  Add #(.Bits(3)) add_1 (.a(A), .b(B), .c_i(1'b0), .s(add_1_s), .c_o(add_1_c_o));
  and and_1 (and_1_out, add_1_s[2], add_1_s[0]);
  and and_2 (and_2_out, add_1_s[2], add_1_s[1]);
  or or_1 (or_1_out, add_1_c_o, and_1_out, and_2_out);
  not not_1 (not_1_out, or_1_out);
  Seven_Seg seven_seg_1 (
    .a(not_1_out), .b(1'b1), .c(1'b1), .d(not_1_out), .e(not_1_out), .f(not_1_out), .g(1'b0), .dp(1'b0));
endmodule
